// Logisim project Mastermind.circ as structural Verilog: 22 circuits, main circuit main
module main (
  input  in_1,
  input  STOP,
  input  RESET_DEL_SEME,
  output out_4
);

  wire and_1_out, C1, C2, C3, C4, C5, C6, C7, C8, C9, Conferma, Invisibile, multiplexer_1_out, New_Game,
       or_1_out, or_2_out, or_3_out, P_1, p_1_t, P_2, p_2_t, P_3, p_3_t, P_4, p_4_t, Prossimo, Reset_D,
       Reset_M_C, risultato_confronto_1_rosso_1, risultato_confronto_1_rosso_2,
       risultato_confronto_1_rosso_3, risultato_confronto_1_rosso_4, risultato_confronto_1_verde_1,
       risultato_confronto_1_verde_2, risultato_confronto_1_verde_3, risultato_confronto_1_verde_4,
       risultato_confronto_2_rosso_1, risultato_confronto_2_rosso_2, risultato_confronto_2_rosso_3,
       risultato_confronto_2_rosso_4, risultato_confronto_2_verde_1, risultato_confronto_2_verde_2,
       risultato_confronto_2_verde_3, risultato_confronto_2_verde_4, risultato_confronto_3_rosso_1,
       risultato_confronto_3_rosso_2, risultato_confronto_3_rosso_3, risultato_confronto_3_rosso_4,
       risultato_confronto_3_verde_1, risultato_confronto_3_verde_2, risultato_confronto_3_verde_3,
       risultato_confronto_3_verde_4, risultato_confronto_4_rosso_1, risultato_confronto_4_rosso_2,
       risultato_confronto_4_rosso_3, risultato_confronto_4_rosso_4, risultato_confronto_4_verde_1,
       risultato_confronto_4_verde_2, risultato_confronto_4_verde_3, risultato_confronto_4_verde_4,
       risultato_confronto_5_rosso_1, risultato_confronto_5_rosso_2, risultato_confronto_5_rosso_3,
       risultato_confronto_5_rosso_4, risultato_confronto_5_verde_1, risultato_confronto_5_verde_2,
       risultato_confronto_5_verde_3, risultato_confronto_5_verde_4, risultato_confronto_6_rosso_1,
       risultato_confronto_6_rosso_2, risultato_confronto_6_rosso_3, risultato_confronto_6_rosso_4,
       risultato_confronto_6_verde_1, risultato_confronto_6_verde_2, risultato_confronto_6_verde_3,
       risultato_confronto_6_verde_4, risultato_confronto_7_rosso_1, risultato_confronto_7_rosso_2,
       risultato_confronto_7_rosso_3, risultato_confronto_7_rosso_4, risultato_confronto_7_verde_1,
       risultato_confronto_7_verde_2, risultato_confronto_7_verde_3, risultato_confronto_7_verde_4,
       risultato_confronto_8_rosso_1, risultato_confronto_8_rosso_2, risultato_confronto_8_rosso_3,
       risultato_confronto_8_rosso_4, risultato_confronto_8_verde_1, risultato_confronto_8_verde_2,
       risultato_confronto_8_verde_3, risultato_confronto_8_verde_4, risultato_confronto_9_rosso_1,
       risultato_confronto_9_rosso_2, risultato_confronto_9_rosso_3, risultato_confronto_9_rosso_4,
       risultato_confronto_9_verde_1, risultato_confronto_9_verde_2, risultato_confronto_9_verde_3,
       risultato_confronto_9_verde_4, S1, S2, S3, S4, S5, S6, S7, S8, S9, Salva, Salvataggio, Sconfitta,
       Selettore_C, Selettore_D, serie_non_uguale_1_sconfitta, Switch_C, Switch_D, V1, V2, V3, V4, V5, V6,
       V7, V8, V9, Vittoria;
  wire [3:0] N_1, N_2, N_3, N_4, nascondi_codice_codificatore_1_out_6, nascondi_codice_codificatore_1_out_7,
       nascondi_codice_codificatore_1_out_8, nascondi_codice_codificatore_1_out_9,
       scelta_decodificatore_1_out_10, scelta_decodificatore_1_out_11, scelta_decodificatore_1_out_12,
       scelta_decodificatore_1_out_13, scelta_decodificatore_1_out_14, scelta_decodificatore_1_out_15,
       scelta_decodificatore_1_out_16, scelta_decodificatore_1_out_17, scelta_decodificatore_1_out_18,
       scelta_decodificatore_1_out_19, scelta_decodificatore_1_out_20, scelta_decodificatore_1_out_21,
       scelta_decodificatore_1_out_22, scelta_decodificatore_1_out_23, scelta_decodificatore_1_out_24,
       scelta_decodificatore_1_out_25, scelta_decodificatore_1_out_26, scelta_decodificatore_1_out_27,
       scelta_decodificatore_1_out_28, scelta_decodificatore_1_out_29, scelta_decodificatore_1_out_30,
       scelta_decodificatore_1_out_31, scelta_decodificatore_1_out_32, scelta_decodificatore_1_out_33,
       scelta_decodificatore_1_out_34, scelta_decodificatore_1_out_35, scelta_decodificatore_1_out_36,
       scelta_decodificatore_1_out_37, scelta_decodificatore_1_out_38, scelta_decodificatore_1_out_39,
       scelta_decodificatore_1_out_40, scelta_decodificatore_1_out_41, scelta_decodificatore_1_out_42,
       scelta_decodificatore_1_out_43, scelta_decodificatore_1_out_44, scelta_decodificatore_1_out_45;

  LED led_1 (.in(Vittoria));
  LED led_2 (.in(Vittoria));
  LED led_3 (.in(Vittoria));
  LED led_4 (.in(Vittoria));
  LED led_5 (.in(Vittoria));
  Hex_Digit_Display hex_digit_display_1 (.value(nascondi_codice_codificatore_1_out_6));  // open: dp
  Nascondi_Codice_Codificatore nascondi_codice_codificatore_1 (
    .in_1(N_1), .Pulsante(Invisibile), .out_6(nascondi_codice_codificatore_1_out_6), .in_3(N_2),
    .out_7(nascondi_codice_codificatore_1_out_7), .in_4(N_3), .out_8(nascondi_codice_codificatore_1_out_8),
    .in_5(N_4), .out_9(nascondi_codice_codificatore_1_out_9));
  DotMatrix #(.matrixcols(1), .matrixrows(1)) dotmatrix_1 (.col0(p_1_t));
  LED led_6 (.in(Vittoria));
  LED led_7 (.in(Vittoria));
  Hex_Digit_Display hex_digit_display_2 (.value(nascondi_codice_codificatore_1_out_7));  // open: dp
  Hex_Digit_Display hex_digit_display_3 (.value(nascondi_codice_codificatore_1_out_8));  // open: dp
  DotMatrix #(.matrixcols(1), .matrixrows(1)) dotmatrix_2 (.col0(p_2_t));
  DotMatrix #(.matrixcols(1), .matrixrows(1)) dotmatrix_3 (.col0(p_3_t));
  LED led_8 (.in(Sconfitta));
  LED led_9 (.in(Sconfitta));
  LED led_10 (.in(Sconfitta));
  LED led_11 (.in(Sconfitta));
  Hex_Digit_Display hex_digit_display_4 (.value(nascondi_codice_codificatore_1_out_9));  // open: dp
  DotMatrix #(.matrixcols(1), .matrixrows(1)) dotmatrix_4 (.col0(p_4_t));
  LED led_12 (.in(Sconfitta));
  LED led_13 (.in(Sconfitta));
  LED led_14 (.in(Sconfitta));
  LED led_15 (.in(Sconfitta));
  Button NASCONDI_CODICE (.out(Invisibile));
  Button SALVA_CODICE (.out(Salvataggio));
  Button CAMBIO_CIFRA (.out(Switch_C));
  Button INCREMENTO_POSIZIONE (.out(Selettore_C));
  Button RESET_A_ZERO_POSIZIONE (.out(Reset_M_C));
  Scelta_Codificatore scelta_codificatore_1 (
    .RESET(RESET_DEL_SEME), .STOP(STOP), .SELETTORE(in_1), .SWITCH_POSIZIONE(Switch_C),
    .SELETTORE_2(Selettore_C), .out_9(N_1), .out_10(N_2), .out_11(N_3), .out_12(N_4), .out_17(p_4_t),
    .out_16(p_3_t), .out_15(p_2_t), .out_14(p_1_t), .AZZERAMENTO(Reset_M_C), .SALVA(Salvataggio),
    .SALVATAGGIO_RIUSCITO(out_4), .RESET_SALVATAGGIO(New_Game));
  Button RESET_PARTITA (.out(New_Game));
  Hex_Digit_Display hex_digit_display_5 (.value(scelta_decodificatore_1_out_12));  // open: dp
  Hex_Digit_Display hex_digit_display_6 (.value(scelta_decodificatore_1_out_10));  // open: dp
  Hex_Digit_Display hex_digit_display_7 (.value(scelta_decodificatore_1_out_20));  // open: dp
  Hex_Digit_Display hex_digit_display_8 (.value(scelta_decodificatore_1_out_18));  // open: dp
  Hex_Digit_Display hex_digit_display_9 (.value(scelta_decodificatore_1_out_28));  // open: dp
  Hex_Digit_Display hex_digit_display_10 (.value(scelta_decodificatore_1_out_26));  // open: dp
  Hex_Digit_Display hex_digit_display_11 (.value(scelta_decodificatore_1_out_36));  // open: dp
  Hex_Digit_Display hex_digit_display_12 (.value(scelta_decodificatore_1_out_34));  // open: dp
  Hex_Digit_Display hex_digit_display_13 (.value(scelta_decodificatore_1_out_42));  // open: dp
  Hex_Digit_Display hex_digit_display_14 (.value(scelta_decodificatore_1_out_43));  // open: dp
  Hex_Digit_Display hex_digit_display_15 (.value(scelta_decodificatore_1_out_14));  // open: dp
  Hex_Digit_Display hex_digit_display_16 (.value(scelta_decodificatore_1_out_22));  // open: dp
  Hex_Digit_Display hex_digit_display_17 (.value(scelta_decodificatore_1_out_30));  // open: dp
  Hex_Digit_Display hex_digit_display_18 (.value(scelta_decodificatore_1_out_38));  // open: dp
  Hex_Digit_Display hex_digit_display_19 (.value(scelta_decodificatore_1_out_44));  // open: dp
  Hex_Digit_Display hex_digit_display_20 (.value(scelta_decodificatore_1_out_16));  // open: dp
  Hex_Digit_Display hex_digit_display_21 (.value(scelta_decodificatore_1_out_24));  // open: dp
  Hex_Digit_Display hex_digit_display_22 (.value(scelta_decodificatore_1_out_32));  // open: dp
  Hex_Digit_Display hex_digit_display_23 (.value(scelta_decodificatore_1_out_40));  // open: dp
  Hex_Digit_Display hex_digit_display_24 (.value(scelta_decodificatore_1_out_45));  // open: dp
  LED led_16 (.in(risultato_confronto_1_verde_1));
  LED led_17 (.in(risultato_confronto_1_rosso_1));
  LED led_18 (.in(risultato_confronto_1_rosso_3));
  LED led_19 (.in(risultato_confronto_1_verde_3));
  LED led_20 (.in(risultato_confronto_2_rosso_1));
  LED led_21 (.in(risultato_confronto_2_verde_1));
  LED led_22 (.in(risultato_confronto_2_rosso_3));
  LED led_23 (.in(risultato_confronto_2_verde_3));
  LED led_24 (.in(risultato_confronto_3_rosso_1));
  LED led_25 (.in(risultato_confronto_3_verde_1));
  LED led_26 (.in(risultato_confronto_3_rosso_3));
  LED led_27 (.in(risultato_confronto_3_verde_3));
  LED led_28 (.in(risultato_confronto_4_verde_1));
  LED led_29 (.in(risultato_confronto_4_rosso_1));
  LED led_30 (.in(risultato_confronto_4_verde_3));
  LED led_31 (.in(risultato_confronto_4_rosso_3));
  LED led_32 (.in(risultato_confronto_5_rosso_1));
  LED led_33 (.in(risultato_confronto_5_verde_1));
  LED led_34 (.in(risultato_confronto_5_verde_3));
  LED led_35 (.in(risultato_confronto_5_rosso_3));
  Multiplexer multiplexer_1 (.in0(1'b0), .in1(and_1_out), .out(multiplexer_1_out), .sel(out_4));  // open: en
  and and_1 (and_1_out, Switch_D, ~Vittoria, ~Sconfitta);  // AND_Gate
  or or_1 (or_1_out, Salva, New_Game);
  LED led_36 (.in(risultato_confronto_1_rosso_2));
  LED led_37 (.in(risultato_confronto_1_verde_2));
  Risultato_Confronto risultato_confronto_1 (
    .in_1(N_1), .in_2(N_2), .in_3(N_3), .in_4(N_4), .in_6(scelta_decodificatore_1_out_10),
    .in_7(scelta_decodificatore_1_out_12), .in_8(scelta_decodificatore_1_out_14),
    .in_9(scelta_decodificatore_1_out_16), .VERDE_1(risultato_confronto_1_verde_1),
    .ROSSO_1(risultato_confronto_1_rosso_1), .VERDE_2(risultato_confronto_1_verde_2),
    .ROSSO_2(risultato_confronto_1_rosso_2), .VITTORIA(V1), .VERDE_3(risultato_confronto_1_verde_3),
    .PROSSIMI_SLOT(S1), .VERDE_4(risultato_confronto_1_verde_4), .ROSSO_4(risultato_confronto_1_rosso_4),
    .PULSANTE(C1), .RESET(New_Game), .ROSSO_3(risultato_confronto_1_rosso_3));
  LED led_38 (.in(risultato_confronto_1_rosso_4));
  LED led_39 (.in(risultato_confronto_1_verde_4));
  LED led_40 (.in(risultato_confronto_2_rosso_2));
  LED led_41 (.in(risultato_confronto_2_verde_2));
  Risultato_Confronto risultato_confronto_2 (
    .in_1(N_1), .in_2(N_2), .in_3(N_3), .in_4(N_4), .in_6(scelta_decodificatore_1_out_18),
    .in_7(scelta_decodificatore_1_out_20), .in_8(scelta_decodificatore_1_out_22),
    .in_9(scelta_decodificatore_1_out_24), .VERDE_1(risultato_confronto_2_verde_1),
    .ROSSO_1(risultato_confronto_2_rosso_1), .VERDE_2(risultato_confronto_2_verde_2),
    .ROSSO_2(risultato_confronto_2_rosso_2), .VITTORIA(V3), .VERDE_3(risultato_confronto_2_verde_3),
    .PROSSIMI_SLOT(S3), .VERDE_4(risultato_confronto_2_verde_4), .ROSSO_4(risultato_confronto_2_rosso_4),
    .PULSANTE(C3), .RESET(New_Game), .ROSSO_3(risultato_confronto_2_rosso_3));
  LED led_42 (.in(risultato_confronto_2_verde_4));
  LED led_43 (.in(risultato_confronto_2_rosso_4));
  LED led_44 (.in(risultato_confronto_3_rosso_2));
  LED led_45 (.in(risultato_confronto_3_verde_2));
  Risultato_Confronto risultato_confronto_3 (
    .in_1(N_1), .in_2(N_2), .in_3(N_3), .in_4(N_4), .in_6(scelta_decodificatore_1_out_26),
    .in_7(scelta_decodificatore_1_out_28), .in_8(scelta_decodificatore_1_out_30),
    .in_9(scelta_decodificatore_1_out_32), .VERDE_1(risultato_confronto_3_verde_1),
    .ROSSO_1(risultato_confronto_3_rosso_1), .VERDE_2(risultato_confronto_3_verde_2),
    .ROSSO_2(risultato_confronto_3_rosso_2), .VITTORIA(V5), .VERDE_3(risultato_confronto_3_verde_3),
    .PROSSIMI_SLOT(S5), .VERDE_4(risultato_confronto_3_verde_4), .ROSSO_4(risultato_confronto_3_rosso_4),
    .PULSANTE(C5), .RESET(New_Game), .ROSSO_3(risultato_confronto_3_rosso_3));
  LED led_46 (.in(risultato_confronto_3_rosso_4));
  LED led_47 (.in(risultato_confronto_3_verde_4));
  LED led_48 (.in(risultato_confronto_4_rosso_2));
  LED led_49 (.in(risultato_confronto_4_verde_2));
  Risultato_Confronto risultato_confronto_4 (
    .in_1(N_1), .in_2(N_2), .in_3(N_3), .in_4(N_4), .in_6(scelta_decodificatore_1_out_34),
    .in_7(scelta_decodificatore_1_out_36), .in_8(scelta_decodificatore_1_out_38),
    .in_9(scelta_decodificatore_1_out_40), .VERDE_1(risultato_confronto_4_verde_1),
    .ROSSO_1(risultato_confronto_4_rosso_1), .VERDE_2(risultato_confronto_4_verde_2),
    .ROSSO_2(risultato_confronto_4_rosso_2), .VITTORIA(V7), .VERDE_3(risultato_confronto_4_verde_3),
    .PROSSIMI_SLOT(S7), .VERDE_4(risultato_confronto_4_verde_4), .ROSSO_4(risultato_confronto_4_rosso_4),
    .PULSANTE(C7), .RESET(New_Game), .ROSSO_3(risultato_confronto_4_rosso_3));
  LED led_50 (.in(risultato_confronto_4_rosso_4));
  LED led_51 (.in(risultato_confronto_4_verde_4));
  LED led_52 (.in(risultato_confronto_5_verde_2));
  LED led_53 (.in(risultato_confronto_5_rosso_2));
  Risultato_Confronto risultato_confronto_5 (
    .in_1(N_1), .in_2(N_2), .in_3(N_3), .in_4(N_4), .in_6(scelta_decodificatore_1_out_42),
    .in_7(scelta_decodificatore_1_out_43), .in_8(scelta_decodificatore_1_out_44),
    .in_9(scelta_decodificatore_1_out_45), .VERDE_1(risultato_confronto_5_verde_1),
    .ROSSO_1(risultato_confronto_5_rosso_1), .VERDE_2(risultato_confronto_5_verde_2),
    .ROSSO_2(risultato_confronto_5_rosso_2), .VITTORIA(V9), .VERDE_3(risultato_confronto_5_verde_3),
    .PROSSIMI_SLOT(S9), .VERDE_4(risultato_confronto_5_verde_4), .ROSSO_4(risultato_confronto_5_rosso_4),
    .PULSANTE(C9), .RESET(New_Game), .ROSSO_3(risultato_confronto_5_rosso_3));
  LED led_54 (.in(risultato_confronto_5_rosso_4));
  LED led_55 (.in(risultato_confronto_5_verde_4));
  Switch_Posizioni_a_4 switch_posizioni_a_4_1 (
    .PULSANTE(multiplexer_1_out), .out_3(P_4), .out_4(P_1), .out_5(P_2), .out_6(P_3), .RESET(or_1_out));
  or or_2 (or_2_out, Vittoria, Sconfitta);
  Scelta_Decodificatore scelta_decodificatore_1 (
    .SWITCH_POSIZIONE(Switch_D), .SELETTORE(Selettore_D), .AZZERAMENTO(Reset_D), .RESET_PARTITA(New_Game),
    .in_8(Prossimo), .out_10(scelta_decodificatore_1_out_10), .out_11(scelta_decodificatore_1_out_11),
    .out_12(scelta_decodificatore_1_out_12), .out_13(scelta_decodificatore_1_out_13),
    .out_14(scelta_decodificatore_1_out_14), .out_15(scelta_decodificatore_1_out_15),
    .out_16(scelta_decodificatore_1_out_16), .out_17(scelta_decodificatore_1_out_17),
    .out_18(scelta_decodificatore_1_out_18), .out_19(scelta_decodificatore_1_out_19),
    .out_20(scelta_decodificatore_1_out_20), .out_21(scelta_decodificatore_1_out_21),
    .out_22(scelta_decodificatore_1_out_22), .out_23(scelta_decodificatore_1_out_23),
    .out_24(scelta_decodificatore_1_out_24), .out_25(scelta_decodificatore_1_out_25),
    .out_26(scelta_decodificatore_1_out_26), .out_27(scelta_decodificatore_1_out_27),
    .out_28(scelta_decodificatore_1_out_28), .out_29(scelta_decodificatore_1_out_29),
    .out_30(scelta_decodificatore_1_out_30), .out_31(scelta_decodificatore_1_out_31),
    .out_32(scelta_decodificatore_1_out_32), .out_33(scelta_decodificatore_1_out_33),
    .out_34(scelta_decodificatore_1_out_34), .out_35(scelta_decodificatore_1_out_35),
    .out_36(scelta_decodificatore_1_out_36), .out_37(scelta_decodificatore_1_out_37),
    .out_38(scelta_decodificatore_1_out_38), .out_39(scelta_decodificatore_1_out_39),
    .out_40(scelta_decodificatore_1_out_40), .out_41(scelta_decodificatore_1_out_41),
    .out_42(scelta_decodificatore_1_out_42), .out_43(scelta_decodificatore_1_out_43),
    .out_44(scelta_decodificatore_1_out_44), .out_45(scelta_decodificatore_1_out_45),
    .PULSANTE_SALVA_INSERIMENTO(Salva), .PASSAGGIO_DI_SERIE(Prossimo), .SALVATAGGIO_RIUSCITO(out_4),
    .VITTORIA_SCONFITTA(or_3_out));
  Blocco_Inserimento_a_9 blocco_inserimento_a_9_1 (
    .PULSANTE(Conferma), ._2(C2), ._3(C3), ._1(C1), ._4(C4), ._5(C5), ._6(C6), ._7(C7), ._8(C8), ._9(C9),
    .SALVATAGGIO(out_4), .SALVA(Salva), .VITTORIA_SCONFITTA(or_2_out), .RESET(New_Game));
  Hex_Digit_Display hex_digit_display_25 (.value(scelta_decodificatore_1_out_11));  // open: dp
  Hex_Digit_Display hex_digit_display_26 (.value(scelta_decodificatore_1_out_19));  // open: dp
  Hex_Digit_Display hex_digit_display_27 (.value(scelta_decodificatore_1_out_27));  // open: dp
  or or_3 (or_3_out, Vittoria, Sconfitta);
  Hex_Digit_Display hex_digit_display_28 (.value(scelta_decodificatore_1_out_37));  // open: dp
  Hex_Digit_Display hex_digit_display_29 (.value(scelta_decodificatore_1_out_35));  // open: dp
  Button CAMBIO_CIFRA_2 (.out(Switch_D));
  Button INCREMENTO_POSIZIONE_2 (.out(Selettore_D));
  Button RESET_A_ZERO_POSIZIONE_2 (.out(Reset_D));
  Button CONFERMA_SCELTA (.out(Conferma));
  Hex_Digit_Display hex_digit_display_30 (.value(scelta_decodificatore_1_out_13));  // open: dp
  Hex_Digit_Display hex_digit_display_31 (.value(scelta_decodificatore_1_out_15));  // open: dp
  Hex_Digit_Display hex_digit_display_32 (.value(scelta_decodificatore_1_out_23));  // open: dp
  Hex_Digit_Display hex_digit_display_33 (.value(scelta_decodificatore_1_out_21));  // open: dp
  Hex_Digit_Display hex_digit_display_34 (.value(scelta_decodificatore_1_out_29));  // open: dp
  Hex_Digit_Display hex_digit_display_35 (.value(scelta_decodificatore_1_out_31));  // open: dp
  Hex_Digit_Display hex_digit_display_36 (.value(scelta_decodificatore_1_out_39));  // open: dp
  DotMatrix #(.matrixcols(1), .matrixrows(1)) dotmatrix_5 (.col0(P_2));
  DotMatrix #(.matrixcols(1), .matrixrows(1)) dotmatrix_6 (.col0(P_1));
  Serie_non_uguale serie_non_uguale_1 (
    .VITTORIA_SCONFITTA(or_2_out), .S1(S1), .S2(S2), .S3(S3), .S4(S4), .S5(S5), .S6(S6), .S7(S7), .S8(S8),
    .S9(S9), .PROSSIMO_BLOCCO(Prossimo), .SCONFITTA(serie_non_uguale_1_sconfitta), .RESET(New_Game));
  Hex_Digit_Display hex_digit_display_37 (.value(scelta_decodificatore_1_out_17));  // open: dp
  Hex_Digit_Display hex_digit_display_38 (.value(scelta_decodificatore_1_out_25));  // open: dp
  Hex_Digit_Display hex_digit_display_39 (.value(scelta_decodificatore_1_out_33));  // open: dp
  Hex_Digit_Display hex_digit_display_40 (.value(scelta_decodificatore_1_out_41));  // open: dp
  DotMatrix #(.matrixcols(1), .matrixrows(1)) dotmatrix_7 (.col0(P_3));
  DotMatrix #(.matrixcols(1), .matrixrows(1)) dotmatrix_8 (.col0(P_4));
  LED led_56 (.in(risultato_confronto_6_verde_1));
  LED led_57 (.in(risultato_confronto_6_verde_3));
  LED led_58 (.in(risultato_confronto_7_verde_1));
  LED led_59 (.in(risultato_confronto_7_verde_3));
  LED led_60 (.in(risultato_confronto_8_verde_1));
  LED led_61 (.in(risultato_confronto_8_verde_3));
  LED led_62 (.in(risultato_confronto_9_verde_1));
  LED led_63 (.in(risultato_confronto_9_verde_3));
  LED led_64 (.in(risultato_confronto_6_verde_2));
  LED led_65 (.in(risultato_confronto_6_rosso_1));
  LED led_66 (.in(risultato_confronto_6_verde_4));
  LED led_67 (.in(risultato_confronto_6_rosso_3));
  LED led_68 (.in(risultato_confronto_7_verde_2));
  LED led_69 (.in(risultato_confronto_7_rosso_1));
  LED led_70 (.in(risultato_confronto_7_verde_4));
  LED led_71 (.in(risultato_confronto_7_rosso_3));
  LED led_72 (.in(risultato_confronto_8_verde_2));
  LED led_73 (.in(risultato_confronto_8_rosso_1));
  LED led_74 (.in(risultato_confronto_8_verde_4));
  LED led_75 (.in(risultato_confronto_8_rosso_3));
  LED led_76 (.in(risultato_confronto_9_verde_2));
  LED led_77 (.in(risultato_confronto_9_rosso_2));
  LED led_78 (.in(risultato_confronto_9_rosso_1));
  LED led_79 (.in(risultato_confronto_9_rosso_3));
  LED led_80 (.in(risultato_confronto_9_rosso_4));
  LED led_81 (.in(risultato_confronto_9_verde_4));
  or or_4 (Vittoria, V1, V2, V3, V4, V5, V6, V7, V8, V9);
  and and_2 (Sconfitta, ~Vittoria, serie_non_uguale_1_sconfitta);  // AND_Gate
  LED led_82 (.in(risultato_confronto_6_rosso_2));
  Risultato_Confronto risultato_confronto_6 (
    .in_1(N_1), .in_2(N_2), .in_3(N_3), .in_4(N_4), .in_6(scelta_decodificatore_1_out_11),
    .in_7(scelta_decodificatore_1_out_13), .in_8(scelta_decodificatore_1_out_15),
    .in_9(scelta_decodificatore_1_out_17), .VERDE_1(risultato_confronto_6_verde_1),
    .ROSSO_1(risultato_confronto_6_rosso_1), .VERDE_2(risultato_confronto_6_verde_2),
    .ROSSO_2(risultato_confronto_6_rosso_2), .VITTORIA(V2), .VERDE_3(risultato_confronto_6_verde_3),
    .PROSSIMI_SLOT(S2), .VERDE_4(risultato_confronto_6_verde_4), .ROSSO_4(risultato_confronto_6_rosso_4),
    .PULSANTE(C2), .RESET(New_Game), .ROSSO_3(risultato_confronto_6_rosso_3));
  LED led_83 (.in(risultato_confronto_6_rosso_4));
  LED led_84 (.in(risultato_confronto_7_rosso_2));
  Risultato_Confronto risultato_confronto_7 (
    .in_1(N_1), .in_2(N_2), .in_3(N_3), .in_4(N_4), .in_6(scelta_decodificatore_1_out_19),
    .in_7(scelta_decodificatore_1_out_21), .in_8(scelta_decodificatore_1_out_23),
    .in_9(scelta_decodificatore_1_out_25), .VERDE_1(risultato_confronto_7_verde_1),
    .ROSSO_1(risultato_confronto_7_rosso_1), .VERDE_2(risultato_confronto_7_verde_2),
    .ROSSO_2(risultato_confronto_7_rosso_2), .VITTORIA(V4), .VERDE_3(risultato_confronto_7_verde_3),
    .PROSSIMI_SLOT(S4), .VERDE_4(risultato_confronto_7_verde_4), .ROSSO_4(risultato_confronto_7_rosso_4),
    .PULSANTE(C4), .RESET(New_Game), .ROSSO_3(risultato_confronto_7_rosso_3));
  LED led_85 (.in(risultato_confronto_7_rosso_4));
  LED led_86 (.in(risultato_confronto_8_rosso_2));
  Risultato_Confronto risultato_confronto_8 (
    .in_1(N_1), .in_2(N_2), .in_3(N_3), .in_4(N_4), .in_6(scelta_decodificatore_1_out_27),
    .in_7(scelta_decodificatore_1_out_29), .in_8(scelta_decodificatore_1_out_31),
    .in_9(scelta_decodificatore_1_out_33), .VERDE_1(risultato_confronto_8_verde_1),
    .ROSSO_1(risultato_confronto_8_rosso_1), .VERDE_2(risultato_confronto_8_verde_2),
    .ROSSO_2(risultato_confronto_8_rosso_2), .VITTORIA(V6), .VERDE_3(risultato_confronto_8_verde_3),
    .PROSSIMI_SLOT(S6), .VERDE_4(risultato_confronto_8_verde_4), .ROSSO_4(risultato_confronto_8_rosso_4),
    .PULSANTE(C6), .RESET(New_Game), .ROSSO_3(risultato_confronto_8_rosso_3));
  LED led_87 (.in(risultato_confronto_8_rosso_4));
  Risultato_Confronto risultato_confronto_9 (
    .in_1(N_1), .in_2(N_2), .in_3(N_3), .in_4(N_4), .in_6(scelta_decodificatore_1_out_35),
    .in_7(scelta_decodificatore_1_out_37), .in_8(scelta_decodificatore_1_out_39),
    .in_9(scelta_decodificatore_1_out_41), .VERDE_1(risultato_confronto_9_verde_1),
    .ROSSO_1(risultato_confronto_9_rosso_1), .VERDE_2(risultato_confronto_9_verde_2),
    .ROSSO_2(risultato_confronto_9_rosso_2), .VITTORIA(V8), .VERDE_3(risultato_confronto_9_verde_3),
    .PROSSIMI_SLOT(S8), .VERDE_4(risultato_confronto_9_verde_4), .ROSSO_4(risultato_confronto_9_rosso_4),
    .PULSANTE(C8), .RESET(New_Game), .ROSSO_3(risultato_confronto_9_rosso_3));

  // Other names for the same wires on the sheet: Reset_C = RESET_DEL_SEME; Salvataggio_Riuscito = out_4;
  //   Scelta = in_1

  // Notes on the sheet:
  //   0 = Scelta casuale
  //   1 = Scelta manuale
  //   CONTROLLI CODIFICATORE
  //   Comandi scelta casuale
  //   Comandi scelta manuale
  //   CONTROLLI  DECODIFICATORE
  //   POSIZIONE CORRENtE
endmodule

module Scelta_Codificatore (
  input  RESET,
  input  SALVA,
  input  STOP,
  input  SELETTORE,
  input  SWITCH_POSIZIONE,
  input  SELETTORE_2,
  input  RESET_SALVATAGGIO,
  input  AZZERAMENTO,
  output [3:0] out_9,
  output [3:0] out_10,
  output [3:0] out_11,
  output [3:0] out_12,
  output SALVATAGGIO_RIUSCITO,
  output out_14,
  output out_15,
  output out_16,
  output out_17
);

  wire and_1_out, and_2_out, and_3_out, and_4_out, and_5_out, filtro_1_out_2, filtro_2_out_2, filtro_3_out_2,
       filtro_4_out_2, multiplexer_1_out, multiplexer_2_out, multiplexer_3_out, multiplexer_4_out,
       multiplexer_5_out, multiplexer_6_out, multiplexer_7_out, multiplexer_8_out, multiplexer_9_out,
       multiplexer_10_out, or_1_out, or_2_out, or_3_out, or_4_out, or_5_out;
  wire [3:0] M_1, M_2, M_3, M_4, multiplexer_11_out, multiplexer_12_out, multiplexer_13_out,
       multiplexer_14_out, R_1, R_2, R_3, R_4;

  Multiplexer multiplexer_1 (.in0(STOP), .in1(1'b1), .out(multiplexer_1_out), .sel(SELETTORE));  // open: en
  Multiplexer multiplexer_2 (.in0(1'b0), .in1(SELETTORE_2), .out(multiplexer_2_out), .sel(SELETTORE));  // open: en
  Generatore_di_numeri generatore_di_numeri_1 (
    .RESET(RESET), .STOP(multiplexer_1_out), .out_3(R_1), .out_4(R_2), .out_5(R_3), .out_6(R_4));
  Multiplexer multiplexer_3 (.in0(1'b0), .in1(SWITCH_POSIZIONE), .out(multiplexer_3_out), .sel(SELETTORE));  // open: en
  Switch_Posizioni_a_4 switch_posizioni_a_4_1 (
    .PULSANTE(multiplexer_3_out), .out_3(out_17), .out_4(out_14), .out_5(out_15), .out_6(out_16),
    .RESET(RESET_SALVATAGGIO));
  Multiplexer multiplexer_4 (.in0(1'b0), .in1(multiplexer_2_out), .out(multiplexer_4_out), .sel(out_17));  // open: en
  Multiplexer multiplexer_5 (.in0(1'b0), .in1(AZZERAMENTO), .out(multiplexer_5_out), .sel(SELETTORE));  // open: en
  Multiplexer multiplexer_6 (.in0(1'b0), .in1(multiplexer_2_out), .out(multiplexer_6_out), .sel(out_14));  // open: en
  Multiplexer multiplexer_7 (.in0(1'b0), .in1(multiplexer_2_out), .out(multiplexer_7_out), .sel(out_15));  // open: en
  Multiplexer multiplexer_8 (.in0(1'b0), .in1(multiplexer_2_out), .out(multiplexer_8_out), .sel(out_16));  // open: en
  Multiplexer multiplexer_9 (.in0(STOP), .in1(1'b1), .out(multiplexer_9_out), .sel(SELETTORE));  // open: en
  and and_1 (and_1_out, out_14, multiplexer_5_out);
  and and_2 (and_2_out, out_15, multiplexer_5_out);
  and and_3 (and_3_out, out_16, multiplexer_5_out);
  and and_4 (and_4_out, out_17, multiplexer_5_out);
  Filtro filtro_1 (.Utente(R_1), .out_2(filtro_1_out_2));
  Filtro filtro_2 (.Utente(R_2), .out_2(filtro_2_out_2));
  Filtro filtro_3 (.Utente(R_3), .out_2(filtro_3_out_2));
  Filtro filtro_4 (.Utente(R_4), .out_2(filtro_4_out_2));
  Selettore selettore_1 (.Pulsante(multiplexer_6_out), .Reset_Manuale(or_1_out), .out_3(M_1));
  or or_1 (or_1_out, and_1_out, RESET_SALVATAGGIO);
  Selettore u_selettore_2 (.Pulsante(multiplexer_7_out), .Reset_Manuale(or_2_out), .out_3(M_2));
  or or_2 (or_2_out, and_2_out, RESET_SALVATAGGIO);
  Selettore selettore_3 (.Pulsante(multiplexer_8_out), .Reset_Manuale(or_3_out), .out_3(M_3));
  or or_3 (or_3_out, and_3_out, RESET_SALVATAGGIO);
  Selettore selettore_4 (.Pulsante(multiplexer_4_out), .Reset_Manuale(or_4_out), .out_3(M_4));
  or or_4 (or_4_out, and_4_out, RESET_SALVATAGGIO);
  or or_5 (or_5_out, filtro_1_out_2, filtro_2_out_2, filtro_3_out_2, filtro_4_out_2);
  Multiplexer multiplexer_10 (.in0(or_5_out), .in1(1'b0), .out(multiplexer_10_out), .sel(SELETTORE));  // open: en
  and and_5 (and_5_out, multiplexer_9_out, ~multiplexer_10_out, SALVA);  // AND_Gate
  D_Flip_Flop d_ff_1 (.Q(SALVATAGGIO_RIUSCITO), .preset(and_5_out), .reset(RESET_SALVATAGGIO));  // open: clk, D, Qn, en
  Hex_Digit_Display hex_digit_display_1 (.value(out_9));  // open: dp
  Salva_Scelta_Codificatore salva_scelta_codificatore_1 (
    .Reset(RESET_SALVATAGGIO), .Pulsante(and_5_out), .in_3(multiplexer_11_out), .in_4(multiplexer_12_out),
    .in_5(multiplexer_13_out), .in_6(multiplexer_14_out), .out_7(out_9), .out_9(out_11), .out_10(out_12),
    .out_8(out_10));
  Multiplexer #(.width(4)) multiplexer_11 (
    .in0(R_1), .in1(M_1), .out(multiplexer_11_out), .sel(SELETTORE));  // open: en
  Hex_Digit_Display hex_digit_display_2 (.value(out_10));  // open: dp
  Multiplexer #(.width(4)) multiplexer_12 (
    .in0(R_2), .in1(M_2), .out(multiplexer_12_out), .sel(SELETTORE));  // open: en
  Hex_Digit_Display hex_digit_display_3 (.value(out_11));  // open: dp
  Multiplexer #(.width(4)) multiplexer_13 (
    .in0(R_3), .in1(M_3), .out(multiplexer_13_out), .sel(SELETTORE));  // open: en
  Hex_Digit_Display hex_digit_display_4 (.value(out_12));  // open: dp
  Multiplexer #(.width(4)) multiplexer_14 (
    .in0(R_4), .in1(M_4), .out(multiplexer_14_out), .sel(SELETTORE));  // open: en
endmodule

module Scelta_Decodificatore (
  input  VITTORIA_SCONFITTA,
  input  SALVATAGGIO_RIUSCITO,
  input  SWITCH_POSIZIONE,
  input  SELETTORE,
  input  AZZERAMENTO,
  input  PASSAGGIO_DI_SERIE,
  input  RESET_PARTITA,
  input  in_8,
  input  PULSANTE_SALVA_INSERIMENTO,
  output [3:0] out_10,
  output [3:0] out_11,
  output [3:0] out_12,
  output [3:0] out_13,
  output [3:0] out_14,
  output [3:0] out_15,
  output [3:0] out_16,
  output [3:0] out_17,
  output [3:0] out_18,
  output [3:0] out_19,
  output [3:0] out_20,
  output [3:0] out_21,
  output [3:0] out_22,
  output [3:0] out_23,
  output [3:0] out_24,
  output [3:0] out_25,
  output [3:0] out_26,
  output [3:0] out_27,
  output [3:0] out_28,
  output [3:0] out_29,
  output [3:0] out_30,
  output [3:0] out_31,
  output [3:0] out_32,
  output [3:0] out_33,
  output [3:0] out_34,
  output [3:0] out_35,
  output [3:0] out_36,
  output [3:0] out_37,
  output [3:0] out_38,
  output [3:0] out_39,
  output [3:0] out_40,
  output [3:0] out_41,
  output [3:0] out_42,
  output [3:0] out_43,
  output [3:0] out_44,
  output [3:0] out_45
);

  wire and_2_out, and_3_out, and_4_out, and_5_out, and_6_out, and_7_out, and_8_out, and_9_out, and_10_out,
       and_11_out, and_12_out, and_13_out, and_14_out, Blocco, blocco_inserimento_a_4_1_out_7,
       blocco_inserimento_a_4_2_out_7, blocco_inserimento_a_4_3_out_7, blocco_inserimento_a_4_4_out_7,
       blocco_inserimento_a_4_5_out_7, blocco_inserimento_a_4_6_out_7, blocco_inserimento_a_4_7_out_7,
       blocco_inserimento_a_4_8_out_7, blocco_inserimento_a_4_9_out_7, d_ff_1_q, d_ff_1_qn, d_ff_2_q,
       d_ff_2_qn, multiplexer_1_out, multiplexer_2_out, multiplexer_3_out, multiplexer_4_out,
       multiplexer_5_out, multiplexer_6_out, multiplexer_7_out, multiplexer_8_out, multiplexer_9_out,
       multiplexer_10_out, multiplexer_11_out, not_1_out, not_2_out, not_3_out, or_1_out, or_2_out, or_3_out,
       or_4_out, or_5_out, or_6_out, switch_posizione_a_9_1_out_4, switch_posizione_a_9_1_out_5,
       switch_posizione_a_9_1_out_6, switch_posizione_a_9_1_out_7, switch_posizione_a_9_1_out_8,
       switch_posizione_a_9_1_out_9, switch_posizione_a_9_1_out_10, switch_posizione_a_9_1_out_11,
       switch_posizione_a_9_1_out_12, switch_posizioni_a_4_1_out_3, switch_posizioni_a_4_1_out_4,
       switch_posizioni_a_4_1_out_5, switch_posizioni_a_4_1_out_6, undriven, V2, V3, V4, V5, V6, V7, V8, V9;
  wire [3:0] blocco_inserimento_a_4_1_out_8, blocco_inserimento_a_4_1_out_9, blocco_inserimento_a_4_1_out_10,
       blocco_inserimento_a_4_1_out_11, blocco_inserimento_a_4_2_out_8, blocco_inserimento_a_4_2_out_9,
       blocco_inserimento_a_4_2_out_10, blocco_inserimento_a_4_2_out_11, blocco_inserimento_a_4_3_out_8,
       blocco_inserimento_a_4_3_out_9, blocco_inserimento_a_4_3_out_10, blocco_inserimento_a_4_3_out_11,
       blocco_inserimento_a_4_4_out_8, blocco_inserimento_a_4_4_out_9, blocco_inserimento_a_4_4_out_10,
       blocco_inserimento_a_4_4_out_11, blocco_inserimento_a_4_5_out_8, blocco_inserimento_a_4_5_out_9,
       blocco_inserimento_a_4_5_out_10, blocco_inserimento_a_4_5_out_11, blocco_inserimento_a_4_6_out_8,
       blocco_inserimento_a_4_6_out_9, blocco_inserimento_a_4_6_out_10, blocco_inserimento_a_4_6_out_11,
       blocco_inserimento_a_4_7_out_8, blocco_inserimento_a_4_7_out_9, blocco_inserimento_a_4_7_out_10,
       blocco_inserimento_a_4_7_out_11, blocco_inserimento_a_4_8_out_8, blocco_inserimento_a_4_8_out_9,
       blocco_inserimento_a_4_8_out_10, blocco_inserimento_a_4_8_out_11, blocco_inserimento_a_4_9_out_8,
       blocco_inserimento_a_4_9_out_9, blocco_inserimento_a_4_9_out_10, blocco_inserimento_a_4_9_out_11, N1,
       N2, N3, N4, salva_scelta_decodificatore_2_out_7, salva_scelta_decodificatore_2_out_8,
       salva_scelta_decodificatore_2_out_9, salva_scelta_decodificatore_2_out_10,
       salva_scelta_decodificatore_3_out_7, salva_scelta_decodificatore_3_out_8,
       salva_scelta_decodificatore_3_out_9, salva_scelta_decodificatore_3_out_10,
       salva_scelta_decodificatore_4_out_7, salva_scelta_decodificatore_4_out_8,
       salva_scelta_decodificatore_4_out_9, salva_scelta_decodificatore_4_out_10,
       salva_scelta_decodificatore_5_out_7, salva_scelta_decodificatore_5_out_8,
       salva_scelta_decodificatore_5_out_9, salva_scelta_decodificatore_5_out_10,
       salva_scelta_decodificatore_6_out_7, salva_scelta_decodificatore_6_out_8,
       salva_scelta_decodificatore_6_out_9, salva_scelta_decodificatore_6_out_10,
       salva_scelta_decodificatore_7_out_7, salva_scelta_decodificatore_7_out_8,
       salva_scelta_decodificatore_7_out_9, salva_scelta_decodificatore_7_out_10,
       salva_scelta_decodificatore_8_out_7, salva_scelta_decodificatore_8_out_8,
       salva_scelta_decodificatore_8_out_9, salva_scelta_decodificatore_8_out_10,
       salva_scelta_decodificatore_9_out_7, salva_scelta_decodificatore_9_out_8,
       salva_scelta_decodificatore_9_out_9, salva_scelta_decodificatore_9_out_10;

  or or_1 (or_1_out, RESET_PARTITA, not_2_out);
  and and_1 (Blocco, ~VITTORIA_SCONFITTA, SALVATAGGIO_RIUSCITO);  // AND_Gate
  Multiplexer multiplexer_1 (.in0(1'b0), .in1(SWITCH_POSIZIONE), .out(multiplexer_1_out), .sel(Blocco), .en(undriven));
  Multiplexer multiplexer_2 (.in0(1'b0), .in1(SELETTORE), .out(multiplexer_2_out), .sel(Blocco));  // open: en
  Switch_Posizioni_a_4 switch_posizioni_a_4_1 (
    .PULSANTE(multiplexer_1_out), .out_3(switch_posizioni_a_4_1_out_3), .out_4(switch_posizioni_a_4_1_out_4),
    .out_5(switch_posizioni_a_4_1_out_5), .out_6(switch_posizioni_a_4_1_out_6), .RESET(or_1_out));
  Multiplexer multiplexer_3 (
    .in0(1'b0), .in1(multiplexer_2_out), .out(multiplexer_3_out), .sel(switch_posizioni_a_4_1_out_3));  // open: en
  Multiplexer multiplexer_4 (
    .in0(1'b0), .in1(multiplexer_2_out), .out(multiplexer_4_out), .sel(switch_posizioni_a_4_1_out_4));  // open: en
  Multiplexer multiplexer_5 (
    .in0(1'b0), .in1(multiplexer_2_out), .out(multiplexer_5_out), .sel(switch_posizioni_a_4_1_out_5));  // open: en
  Multiplexer multiplexer_6 (
    .in0(1'b0), .in1(multiplexer_2_out), .out(multiplexer_6_out), .sel(switch_posizioni_a_4_1_out_6));  // open: en
  Multiplexer multiplexer_7 (.in0(1'b0), .in1(in_8), .out(multiplexer_7_out), .sel(Blocco));  // open: en
  Multiplexer multiplexer_8 (.in0(1'b0), .in1(1'b1), .out(multiplexer_8_out), .sel(not_1_out));  // open: en
  and and_2 (and_2_out, switch_posizioni_a_4_1_out_4, AZZERAMENTO);
  and and_3 (and_3_out, switch_posizioni_a_4_1_out_5, AZZERAMENTO);
  and and_4 (and_4_out, switch_posizioni_a_4_1_out_6, AZZERAMENTO);
  and and_5 (and_5_out, switch_posizioni_a_4_1_out_3, AZZERAMENTO);
  D_Flip_Flop #(.trigger("falling")) d_ff_1 (
    .clk(multiplexer_7_out), .D(multiplexer_8_out), .Q(d_ff_1_q), .Qn(d_ff_1_qn), .preset(d_ff_1_qn));  // open: en, reset
  not not_1 (not_1_out, d_ff_1_q);
  or or_2 (or_2_out, and_2_out, or_6_out);
  or or_3 (or_3_out, and_3_out, or_6_out);
  or or_4 (or_4_out, and_4_out, or_6_out);
  or or_5 (or_5_out, and_5_out, or_6_out);
  or or_6 (or_6_out, PULSANTE_SALVA_INSERIMENTO, RESET_PARTITA, multiplexer_9_out);
  Multiplexer multiplexer_9 (.in0(1'b0), .in1(multiplexer_11_out), .out(multiplexer_9_out), .sel(Blocco));  // open: en
  not not_2 (not_2_out, d_ff_1_q);
  Selettore selettore_1 (.Pulsante(multiplexer_4_out), .Reset_Manuale(or_2_out), .out_3(N1));
  Selettore selettore_2 (.Pulsante(multiplexer_5_out), .Reset_Manuale(or_3_out), .out_3(N2));
  Selettore selettore_3 (.Pulsante(multiplexer_6_out), .Reset_Manuale(or_4_out), .out_3(N3));
  Selettore selettore_4 (.Pulsante(multiplexer_3_out), .Reset_Manuale(or_5_out), .out_3(N4));
  Multiplexer multiplexer_10 (.in0(1'b0), .in1(1'b1), .out(multiplexer_10_out), .sel(not_3_out));  // open: en
  not not_3 (not_3_out, d_ff_2_q);
  Multiplexer multiplexer_11 (.in0(1'b0), .in1(not_3_out), .out(multiplexer_11_out), .sel(Blocco));  // open: en
  Switch_Posizione_a_9 switch_posizione_a_9_1 (
    .PULSANTE(not_2_out), .out_4(switch_posizione_a_9_1_out_4), .out_5(switch_posizione_a_9_1_out_5),
    .out_6(switch_posizione_a_9_1_out_6), .out_7(switch_posizione_a_9_1_out_7),
    .out_8(switch_posizione_a_9_1_out_8), .out_9(switch_posizione_a_9_1_out_9),
    .out_10(switch_posizione_a_9_1_out_10), .out_11(switch_posizione_a_9_1_out_11),
    .out_12(switch_posizione_a_9_1_out_12), .RESET(RESET_PARTITA), .VITTORIA_SCONFITTA(1'b0));
  D_Flip_Flop #(.trigger("falling")) d_ff_2 (
    .clk(PASSAGGIO_DI_SERIE), .D(multiplexer_10_out), .Q(d_ff_2_q), .Qn(d_ff_2_qn), .preset(d_ff_2_qn));  // open: en, reset
  Switch_Posizione_a_9 switch_posizione_a_9_2 (
    .PULSANTE(multiplexer_11_out), .out_4(V9), .out_6(V2), .out_7(V3), .out_8(V4), .out_9(V5), .out_10(V6),
    .out_11(V7), .out_12(V8), .RESET(RESET_PARTITA), .VITTORIA_SCONFITTA(1'b0));  // open: out_5
  and and_6 (and_6_out, switch_posizione_a_9_1_out_5, PULSANTE_SALVA_INSERIMENTO);
  Blocco_Inserimento_a_4 blocco_inserimento_a_4_1 (
    .in_2(N1), .in_3(N2), .in_4(N3), .in_5(N4), .in_6(switch_posizione_a_9_1_out_5),
    .out_8(blocco_inserimento_a_4_1_out_8), .out_9(blocco_inserimento_a_4_1_out_9),
    .out_10(blocco_inserimento_a_4_1_out_10), .out_11(blocco_inserimento_a_4_1_out_11),
    .out_7(blocco_inserimento_a_4_1_out_7), .in_1(and_6_out));
  and and_7 (and_7_out, switch_posizione_a_9_1_out_7, PULSANTE_SALVA_INSERIMENTO);
  Blocco_Inserimento_a_4 blocco_inserimento_a_4_2 (
    .in_2(N1), .in_3(N2), .in_4(N3), .in_5(N4), .in_6(switch_posizione_a_9_1_out_7),
    .out_8(blocco_inserimento_a_4_2_out_8), .out_9(blocco_inserimento_a_4_2_out_9),
    .out_10(blocco_inserimento_a_4_2_out_10), .out_11(blocco_inserimento_a_4_2_out_11),
    .out_7(blocco_inserimento_a_4_2_out_7), .in_1(and_7_out));
  and and_8 (and_8_out, switch_posizione_a_9_1_out_9, PULSANTE_SALVA_INSERIMENTO);
  Blocco_Inserimento_a_4 blocco_inserimento_a_4_3 (
    .in_2(N1), .in_3(N2), .in_4(N3), .in_5(N4), .in_6(switch_posizione_a_9_1_out_9),
    .out_8(blocco_inserimento_a_4_3_out_8), .out_9(blocco_inserimento_a_4_3_out_9),
    .out_10(blocco_inserimento_a_4_3_out_10), .out_11(blocco_inserimento_a_4_3_out_11),
    .out_7(blocco_inserimento_a_4_3_out_7), .in_1(and_8_out));
  and and_9 (and_9_out, switch_posizione_a_9_1_out_11, PULSANTE_SALVA_INSERIMENTO);
  Blocco_Inserimento_a_4 blocco_inserimento_a_4_4 (
    .in_2(N1), .in_3(N2), .in_4(N3), .in_5(N4), .in_6(switch_posizione_a_9_1_out_11),
    .out_8(blocco_inserimento_a_4_4_out_8), .out_9(blocco_inserimento_a_4_4_out_9),
    .out_10(blocco_inserimento_a_4_4_out_10), .out_11(blocco_inserimento_a_4_4_out_11),
    .out_7(blocco_inserimento_a_4_4_out_7), .in_1(and_9_out));
  and and_10 (and_10_out, switch_posizione_a_9_1_out_4, PULSANTE_SALVA_INSERIMENTO);
  Blocco_Inserimento_a_4 blocco_inserimento_a_4_5 (
    .in_2(N1), .in_3(N2), .in_4(N3), .in_5(N4), .in_6(switch_posizione_a_9_1_out_4),
    .out_8(blocco_inserimento_a_4_5_out_8), .out_9(blocco_inserimento_a_4_5_out_9),
    .out_10(blocco_inserimento_a_4_5_out_10), .out_11(blocco_inserimento_a_4_5_out_11),
    .out_7(blocco_inserimento_a_4_5_out_7), .in_1(and_10_out));
  Salva_Scelta_Decodificatore salva_scelta_decodificatore_1 (
    .Reset(RESET_PARTITA), .Pulsante(blocco_inserimento_a_4_1_out_7), .in_3(blocco_inserimento_a_4_1_out_8),
    .in_4(blocco_inserimento_a_4_1_out_9), .in_5(blocco_inserimento_a_4_1_out_10),
    .in_6(blocco_inserimento_a_4_1_out_11), .out_7(out_10), .out_8(out_12), .out_9(out_14), .out_10(out_16));
  Nascondi_Codice_Decodificatore nascondi_codice_decodificatore_1 (
    .in_2(salva_scelta_decodificatore_2_out_7), .Pulsante(V3), .in_4(salva_scelta_decodificatore_2_out_8),
    .in_5(salva_scelta_decodificatore_2_out_9), .in_6(salva_scelta_decodificatore_2_out_10), .out_7(out_18),
    .out_8(out_20), .out_9(out_22), .out_10(out_24), .RESET(RESET_PARTITA));
  Salva_Scelta_Decodificatore salva_scelta_decodificatore_2 (
    .Reset(RESET_PARTITA), .Pulsante(blocco_inserimento_a_4_2_out_7), .in_3(blocco_inserimento_a_4_2_out_8),
    .in_4(blocco_inserimento_a_4_2_out_9), .in_5(blocco_inserimento_a_4_2_out_10),
    .in_6(blocco_inserimento_a_4_2_out_11), .out_7(salva_scelta_decodificatore_2_out_7),
    .out_8(salva_scelta_decodificatore_2_out_8), .out_9(salva_scelta_decodificatore_2_out_9),
    .out_10(salva_scelta_decodificatore_2_out_10));
  Salva_Scelta_Decodificatore salva_scelta_decodificatore_3 (
    .Reset(RESET_PARTITA), .Pulsante(blocco_inserimento_a_4_3_out_7), .in_3(blocco_inserimento_a_4_3_out_8),
    .in_4(blocco_inserimento_a_4_3_out_9), .in_5(blocco_inserimento_a_4_3_out_10),
    .in_6(blocco_inserimento_a_4_3_out_11), .out_7(salva_scelta_decodificatore_3_out_7),
    .out_8(salva_scelta_decodificatore_3_out_8), .out_9(salva_scelta_decodificatore_3_out_9),
    .out_10(salva_scelta_decodificatore_3_out_10));
  Nascondi_Codice_Decodificatore nascondi_codice_decodificatore_2 (
    .in_2(salva_scelta_decodificatore_3_out_7), .Pulsante(V5), .in_4(salva_scelta_decodificatore_3_out_8),
    .in_5(salva_scelta_decodificatore_3_out_9), .in_6(salva_scelta_decodificatore_3_out_10), .out_7(out_26),
    .out_8(out_28), .out_9(out_30), .out_10(out_32), .RESET(RESET_PARTITA));
  Salva_Scelta_Decodificatore salva_scelta_decodificatore_4 (
    .Reset(RESET_PARTITA), .Pulsante(blocco_inserimento_a_4_4_out_7), .in_3(blocco_inserimento_a_4_4_out_8),
    .in_4(blocco_inserimento_a_4_4_out_9), .in_5(blocco_inserimento_a_4_4_out_10),
    .in_6(blocco_inserimento_a_4_4_out_11), .out_7(salva_scelta_decodificatore_4_out_7),
    .out_8(salva_scelta_decodificatore_4_out_8), .out_9(salva_scelta_decodificatore_4_out_9),
    .out_10(salva_scelta_decodificatore_4_out_10));
  Nascondi_Codice_Decodificatore nascondi_codice_decodificatore_3 (
    .in_2(salva_scelta_decodificatore_4_out_7), .Pulsante(V7), .in_4(salva_scelta_decodificatore_4_out_8),
    .in_5(salva_scelta_decodificatore_4_out_9), .in_6(salva_scelta_decodificatore_4_out_10), .out_7(out_34),
    .out_8(out_36), .out_9(out_38), .out_10(out_40), .RESET(RESET_PARTITA));
  Nascondi_Codice_Decodificatore nascondi_codice_decodificatore_4 (
    .in_2(salva_scelta_decodificatore_5_out_7), .Pulsante(V9), .in_4(salva_scelta_decodificatore_5_out_8),
    .in_5(salva_scelta_decodificatore_5_out_9), .in_6(salva_scelta_decodificatore_5_out_10), .out_7(out_42),
    .out_8(out_43), .out_9(out_44), .out_10(out_45), .RESET(RESET_PARTITA));
  Salva_Scelta_Decodificatore salva_scelta_decodificatore_5 (
    .Reset(RESET_PARTITA), .Pulsante(blocco_inserimento_a_4_5_out_7), .in_3(blocco_inserimento_a_4_5_out_8),
    .in_4(blocco_inserimento_a_4_5_out_9), .in_5(blocco_inserimento_a_4_5_out_10),
    .in_6(blocco_inserimento_a_4_5_out_11), .out_7(salva_scelta_decodificatore_5_out_7),
    .out_8(salva_scelta_decodificatore_5_out_8), .out_9(salva_scelta_decodificatore_5_out_9),
    .out_10(salva_scelta_decodificatore_5_out_10));
  and and_11 (and_11_out, switch_posizione_a_9_1_out_6, PULSANTE_SALVA_INSERIMENTO);
  Blocco_Inserimento_a_4 blocco_inserimento_a_4_6 (
    .in_2(N1), .in_3(N2), .in_4(N3), .in_5(N4), .in_6(switch_posizione_a_9_1_out_6),
    .out_8(blocco_inserimento_a_4_6_out_8), .out_9(blocco_inserimento_a_4_6_out_9),
    .out_10(blocco_inserimento_a_4_6_out_10), .out_11(blocco_inserimento_a_4_6_out_11),
    .out_7(blocco_inserimento_a_4_6_out_7), .in_1(and_11_out));
  and and_12 (and_12_out, switch_posizione_a_9_1_out_8, PULSANTE_SALVA_INSERIMENTO);
  Blocco_Inserimento_a_4 blocco_inserimento_a_4_7 (
    .in_2(N1), .in_3(N2), .in_4(N3), .in_5(N4), .in_6(switch_posizione_a_9_1_out_8),
    .out_8(blocco_inserimento_a_4_7_out_8), .out_9(blocco_inserimento_a_4_7_out_9),
    .out_10(blocco_inserimento_a_4_7_out_10), .out_11(blocco_inserimento_a_4_7_out_11),
    .out_7(blocco_inserimento_a_4_7_out_7), .in_1(and_12_out));
  and and_13 (and_13_out, switch_posizione_a_9_1_out_10, PULSANTE_SALVA_INSERIMENTO);
  Blocco_Inserimento_a_4 blocco_inserimento_a_4_8 (
    .in_2(N1), .in_3(N2), .in_4(N3), .in_5(N4), .in_6(switch_posizione_a_9_1_out_10),
    .out_8(blocco_inserimento_a_4_8_out_8), .out_9(blocco_inserimento_a_4_8_out_9),
    .out_10(blocco_inserimento_a_4_8_out_10), .out_11(blocco_inserimento_a_4_8_out_11),
    .out_7(blocco_inserimento_a_4_8_out_7), .in_1(and_13_out));
  and and_14 (and_14_out, switch_posizione_a_9_1_out_12, PULSANTE_SALVA_INSERIMENTO);
  Blocco_Inserimento_a_4 blocco_inserimento_a_4_9 (
    .in_2(N1), .in_3(N2), .in_4(N3), .in_5(N4), .in_6(switch_posizione_a_9_1_out_12),
    .out_8(blocco_inserimento_a_4_9_out_8), .out_9(blocco_inserimento_a_4_9_out_9),
    .out_10(blocco_inserimento_a_4_9_out_10), .out_11(blocco_inserimento_a_4_9_out_11),
    .out_7(blocco_inserimento_a_4_9_out_7), .in_1(and_14_out));
  Nascondi_Codice_Decodificatore nascondi_codice_decodificatore_5 (
    .in_2(salva_scelta_decodificatore_6_out_7), .Pulsante(V2), .in_4(salva_scelta_decodificatore_6_out_8),
    .in_5(salva_scelta_decodificatore_6_out_9), .in_6(salva_scelta_decodificatore_6_out_10), .out_7(out_11),
    .out_8(out_13), .out_9(out_15), .out_10(out_17), .RESET(RESET_PARTITA));
  Salva_Scelta_Decodificatore salva_scelta_decodificatore_6 (
    .Reset(RESET_PARTITA), .Pulsante(blocco_inserimento_a_4_6_out_7), .in_3(blocco_inserimento_a_4_6_out_8),
    .in_4(blocco_inserimento_a_4_6_out_9), .in_5(blocco_inserimento_a_4_6_out_10),
    .in_6(blocco_inserimento_a_4_6_out_11), .out_7(salva_scelta_decodificatore_6_out_7),
    .out_8(salva_scelta_decodificatore_6_out_8), .out_9(salva_scelta_decodificatore_6_out_9),
    .out_10(salva_scelta_decodificatore_6_out_10));
  Nascondi_Codice_Decodificatore nascondi_codice_decodificatore_6 (
    .in_2(salva_scelta_decodificatore_7_out_7), .Pulsante(V4), .in_4(salva_scelta_decodificatore_7_out_8),
    .in_5(salva_scelta_decodificatore_7_out_9), .in_6(salva_scelta_decodificatore_7_out_10), .out_7(out_19),
    .out_8(out_21), .out_9(out_23), .out_10(out_25), .RESET(RESET_PARTITA));
  Salva_Scelta_Decodificatore salva_scelta_decodificatore_7 (
    .Reset(RESET_PARTITA), .Pulsante(blocco_inserimento_a_4_7_out_7), .in_3(blocco_inserimento_a_4_7_out_8),
    .in_4(blocco_inserimento_a_4_7_out_9), .in_5(blocco_inserimento_a_4_7_out_10),
    .in_6(blocco_inserimento_a_4_7_out_11), .out_7(salva_scelta_decodificatore_7_out_7),
    .out_8(salva_scelta_decodificatore_7_out_8), .out_9(salva_scelta_decodificatore_7_out_9),
    .out_10(salva_scelta_decodificatore_7_out_10));
  Salva_Scelta_Decodificatore salva_scelta_decodificatore_8 (
    .Reset(RESET_PARTITA), .Pulsante(blocco_inserimento_a_4_8_out_7), .in_3(blocco_inserimento_a_4_8_out_8),
    .in_4(blocco_inserimento_a_4_8_out_9), .in_5(blocco_inserimento_a_4_8_out_10),
    .in_6(blocco_inserimento_a_4_8_out_11), .out_7(salva_scelta_decodificatore_8_out_7),
    .out_8(salva_scelta_decodificatore_8_out_8), .out_9(salva_scelta_decodificatore_8_out_9),
    .out_10(salva_scelta_decodificatore_8_out_10));
  Nascondi_Codice_Decodificatore nascondi_codice_decodificatore_7 (
    .in_2(salva_scelta_decodificatore_8_out_7), .Pulsante(V6), .in_4(salva_scelta_decodificatore_8_out_8),
    .in_5(salva_scelta_decodificatore_8_out_9), .in_6(salva_scelta_decodificatore_8_out_10), .out_7(out_27),
    .out_8(out_29), .out_9(out_31), .out_10(out_33), .RESET(RESET_PARTITA));
  Salva_Scelta_Decodificatore salva_scelta_decodificatore_9 (
    .Reset(RESET_PARTITA), .Pulsante(blocco_inserimento_a_4_9_out_7), .in_3(blocco_inserimento_a_4_9_out_8),
    .in_4(blocco_inserimento_a_4_9_out_9), .in_5(blocco_inserimento_a_4_9_out_10),
    .in_6(blocco_inserimento_a_4_9_out_11), .out_7(salva_scelta_decodificatore_9_out_7),
    .out_8(salva_scelta_decodificatore_9_out_8), .out_9(salva_scelta_decodificatore_9_out_9),
    .out_10(salva_scelta_decodificatore_9_out_10));
  Nascondi_Codice_Decodificatore nascondi_codice_decodificatore_8 (
    .in_2(salva_scelta_decodificatore_9_out_7), .Pulsante(V8), .in_4(salva_scelta_decodificatore_9_out_8),
    .in_5(salva_scelta_decodificatore_9_out_9), .in_6(salva_scelta_decodificatore_9_out_10), .out_7(out_35),
    .out_8(out_37), .out_9(out_39), .out_10(out_41), .RESET(RESET_PARTITA));

  // Other names for the same wires on the sheet: New_Game = RESET_PARTITA; Salvataggio = PULSANTE_SALVA_INSERIMENTO

  // Notes on the sheet:
  //   CAMBIO SERIE SE NON UGUALE ALLA SERIE DEL CODIFICATORE
  //   CAMBIO SERIE
endmodule

module Blocco_Inserimento_a_4 (
  input  in_1,
  input  [3:0] in_2,
  input  [3:0] in_3,
  input  [3:0] in_4,
  input  [3:0] in_5,
  input  in_6,
  output out_7,
  output [3:0] out_8,
  output [3:0] out_9,
  output [3:0] out_10,
  output [3:0] out_11
);

  Multiplexer #(.width(4)) multiplexer_1 (.in0(4'b1111), .in1(in_4), .out(out_10), .sel(in_6));  // open: en
  Multiplexer #(.width(4)) multiplexer_2 (.in0(4'b1111), .in1(in_5), .out(out_11), .sel(in_6));  // open: en
  Multiplexer #(.width(4)) multiplexer_3 (.in0(4'b1111), .in1(in_3), .out(out_9), .sel(in_6));  // open: en
  Multiplexer multiplexer_4 (.in1(in_1), .out(out_7), .sel(in_6));  // open: in0, en
  Multiplexer #(.width(4)) multiplexer_5 (.in0(4'b1111), .in1(in_2), .out(out_8), .sel(in_6));  // open: en
endmodule

module Blocco_Inserimento_a_9 (
  input  VITTORIA_SCONFITTA,
  input  SALVATAGGIO,
  input  PULSANTE,
  input  RESET,
  output _1,
  output _2,
  output _3,
  output _4,
  output _5,
  output _6,
  output _7,
  output _8,
  output _9,
  output SALVA
);

  wire and_1_out, d_ff_1_q, d_ff_1_qn, multiplexer_2_out, multiplexer_3_out, not_1_out,
       switch_posizione_a_9_1_out_4, switch_posizione_a_9_1_out_5, switch_posizione_a_9_1_out_6,
       switch_posizione_a_9_1_out_7, switch_posizione_a_9_1_out_8, switch_posizione_a_9_1_out_9,
       switch_posizione_a_9_1_out_10, switch_posizione_a_9_1_out_11, switch_posizione_a_9_1_out_12;

  and and_1 (and_1_out, ~VITTORIA_SCONFITTA, SALVATAGGIO);  // AND_Gate
  Multiplexer multiplexer_1 (.in0(1'b0), .in1(PULSANTE), .out(SALVA), .sel(and_1_out));  // open: en
  Multiplexer multiplexer_2 (.in0(1'b0), .in1(1'b1), .out(multiplexer_2_out), .sel(not_1_out));  // open: en
  not not_1 (not_1_out, d_ff_1_q);
  D_Flip_Flop #(.trigger("falling")) d_ff_1 (
    .clk(SALVA), .D(multiplexer_2_out), .Q(d_ff_1_q), .Qn(d_ff_1_qn), .preset(d_ff_1_qn));  // open: en, reset
  Multiplexer multiplexer_3 (
    .in0(d_ff_1_qn), .in1(1'b1), .out(multiplexer_3_out), .sel(VITTORIA_SCONFITTA));  // open: en
  Switch_Posizione_a_9 switch_posizione_a_9_1 (
    .PULSANTE(multiplexer_3_out), .out_4(switch_posizione_a_9_1_out_4), .out_5(switch_posizione_a_9_1_out_5),
    .out_6(switch_posizione_a_9_1_out_6), .out_7(switch_posizione_a_9_1_out_7),
    .out_8(switch_posizione_a_9_1_out_8), .out_9(switch_posizione_a_9_1_out_9),
    .out_10(switch_posizione_a_9_1_out_10), .out_11(switch_posizione_a_9_1_out_11),
    .out_12(switch_posizione_a_9_1_out_12), .RESET(RESET), .VITTORIA_SCONFITTA(VITTORIA_SCONFITTA));
  and and_2 (_1, SALVA, switch_posizione_a_9_1_out_5);
  and and_3 (_2, SALVA, switch_posizione_a_9_1_out_6);
  and and_4 (_3, SALVA, switch_posizione_a_9_1_out_7);
  and and_5 (_4, SALVA, switch_posizione_a_9_1_out_8);
  and and_6 (_5, SALVA, switch_posizione_a_9_1_out_9);
  and and_7 (_6, SALVA, switch_posizione_a_9_1_out_10);
  and and_8 (_7, SALVA, switch_posizione_a_9_1_out_11);
  and and_9 (_8, SALVA, switch_posizione_a_9_1_out_12);
  and and_10 (_9, SALVA, switch_posizione_a_9_1_out_4);

  // Other names for the same wires on the sheet: P = SALVA
endmodule

module Filtro (
  input  [3:0] Utente,
  output out_2
);

  wire comparator_1_eq, comparator_2_eq, comparator_3_eq, comparator_4_eq, comparator_5_eq, comparator_6_eq;

  Comparator #(.width(4)) comparator_1 (.a(4'b1010), .b(Utente), .eq(comparator_1_eq));  // open: gt, lt
  Comparator #(.width(4)) comparator_2 (.a(4'b1011), .b(Utente), .eq(comparator_2_eq));  // open: gt, lt
  Comparator #(.width(4)) comparator_3 (.a(4'b1100), .b(Utente), .eq(comparator_3_eq));  // open: gt, lt
  Comparator #(.width(4)) comparator_4 (.a(4'b1101), .b(Utente), .eq(comparator_4_eq));  // open: gt, lt
  Comparator #(.width(4)) comparator_5 (.a(4'b1110), .b(Utente), .eq(comparator_5_eq));  // open: gt, lt
  Comparator #(.width(4)) comparator_6 (.a(4'b1111), .b(Utente), .eq(comparator_6_eq));  // open: gt, lt
  or or_1 (out_2, comparator_1_eq, comparator_2_eq, comparator_3_eq, comparator_4_eq, comparator_5_eq, comparator_6_eq);
endmodule

module Generatore_di_numeri (
  input  RESET,
  input  STOP,
  output [3:0] out_3,
  output [3:0] out_4,
  output [3:0] out_5,
  output [3:0] out_6
);

  wire and_1_out, and_2_out, and_3_out, and_4_out, clock_1_out, filtro_1_out_2, filtro_2_out_2,
       filtro_3_out_2, filtro_4_out_2, not_1_out, not_2_out, not_3_out, not_4_out, or_1_out, or_2_out,
       or_3_out, or_4_out;

  Clock clock_1 (.out(clock_1_out));
  not not_1 (not_1_out, STOP);
  not not_2 (not_2_out, STOP);
  not not_3 (not_3_out, STOP);
  not not_4 (not_4_out, STOP);
  Random #(.width(4), .seed(10)) random_1 (.clk(clock_1_out), .next(or_1_out), .out(out_3), .clr(RESET));
  or or_1 (or_1_out, not_1_out, and_1_out);
  Random #(.width(4), .seed(11)) random_2 (.clk(clock_1_out), .next(or_2_out), .out(out_4), .clr(RESET));
  or or_2 (or_2_out, not_2_out, and_2_out);
  Random #(.width(4), .seed(12)) random_3 (.clk(clock_1_out), .next(or_3_out), .out(out_5), .clr(RESET));
  or or_3 (or_3_out, not_3_out, and_3_out);
  Random #(.width(4), .seed(13)) random_4 (.clk(clock_1_out), .next(or_4_out), .out(out_6), .clr(RESET));
  or or_4 (or_4_out, not_4_out, and_4_out);
  Filtro filtro_1 (.Utente(out_3), .out_2(filtro_1_out_2));
  Filtro filtro_2 (.Utente(out_4), .out_2(filtro_2_out_2));
  Filtro filtro_3 (.Utente(out_5), .out_2(filtro_3_out_2));
  Filtro filtro_4 (.Utente(out_6), .out_2(filtro_4_out_2));
  Hex_Digit_Display hex_digit_display_1 (.value(out_3));  // open: dp
  and and_1 (and_1_out, filtro_1_out_2, STOP);
  Hex_Digit_Display hex_digit_display_2 (.value(out_4));  // open: dp
  and and_2 (and_2_out, filtro_2_out_2, STOP);
  Hex_Digit_Display hex_digit_display_3 (.value(out_5));  // open: dp
  and and_3 (and_3_out, filtro_3_out_2, STOP);
  Hex_Digit_Display hex_digit_display_4 (.value(out_6));  // open: dp
  and and_4 (and_4_out, filtro_4_out_2, STOP);
endmodule

module Selettore (
  input  Pulsante,
  input  Reset_Manuale,
  output [3:0] out_3
);

  wire adder_1_cout, adder_1_out, adder_2_cout, adder_2_out, adder_3_cout, adder_3_out, and_1_out, and_2_out,
       and_3_out, d_ff_1_qn, d_ff_2_qn, d_ff_3_qn, filtro_1_out_2, multiplexer_1_out, multiplexer_2_out,
       multiplexer_3_out, multiplexer_4_out, multiplexer_5_out, multiplexer_6_out, multiplexer_7_out,
       multiplexer_8_out, not_1_out, not_2_out, not_3_out, not_4_out, Reset;

  Multiplexer multiplexer_1 (.in0(1'b0), .in1(1'b1), .out(multiplexer_1_out), .sel(not_1_out));  // open: en
  not not_1 (not_1_out, out_3[0]);
  Multiplexer multiplexer_2 (.in0(1'b0), .in1(Pulsante), .out(multiplexer_2_out), .sel(out_3[0]));  // open: en
  D_Flip_Flop d_ff_1 (
    .clk(Pulsante), .D(multiplexer_1_out), .Q(out_3[0]), .Qn(d_ff_1_qn), .reset(Reset));  // open: preset, en
  Adder #(.width(1)) adder_1 (
    .a(multiplexer_2_out), .b(out_3[0]), .out(adder_1_out), .cout(adder_1_cout));  // open: cin
  and and_1 (and_1_out, adder_1_out, d_ff_1_qn);
  Multiplexer multiplexer_3 (.in0(1'b0), .in1(1'b1), .out(multiplexer_3_out), .sel(not_2_out));  // open: en
  not not_2 (not_2_out, out_3[1]);
  D_Flip_Flop d_ff_2 (
    .clk(and_1_out), .D(multiplexer_3_out), .Q(out_3[1]), .Qn(d_ff_2_qn), .reset(Reset));  // open: preset, en
  Multiplexer multiplexer_4 (.in0(1'b0), .in1(adder_1_cout), .out(multiplexer_4_out), .sel(out_3[1]));  // open: en
  Adder #(.width(1)) adder_2 (
    .a(multiplexer_4_out), .b(out_3[1]), .out(adder_2_out), .cout(adder_2_cout));  // open: cin
  and and_2 (and_2_out, adder_2_out, d_ff_2_qn);
  Multiplexer multiplexer_5 (.in0(1'b0), .in1(1'b1), .out(multiplexer_5_out), .sel(not_3_out));  // open: en
  not not_3 (not_3_out, out_3[2]);
  D_Flip_Flop d_ff_3 (
    .clk(and_2_out), .D(multiplexer_5_out), .Q(out_3[2]), .Qn(d_ff_3_qn), .reset(Reset));  // open: preset, en
  Multiplexer multiplexer_6 (.in0(1'b0), .in1(adder_2_cout), .out(multiplexer_6_out), .sel(out_3[2]));  // open: en
  and and_3 (and_3_out, adder_3_out, d_ff_3_qn);
  Multiplexer multiplexer_7 (.in0(1'b0), .in1(1'b1), .out(multiplexer_7_out), .sel(not_4_out));  // open: en
  Adder #(.width(1)) adder_3 (
    .a(multiplexer_6_out), .b(out_3[2]), .out(adder_3_out), .cout(adder_3_cout));  // open: cin
  D_Flip_Flop d_ff_4 (.clk(and_3_out), .D(multiplexer_7_out), .Q(out_3[3]), .reset(Reset));  // open: Qn, preset, en
  not not_4 (not_4_out, out_3[3]);
  Multiplexer multiplexer_8 (.in0(1'b0), .in1(adder_3_cout), .out(multiplexer_8_out), .sel(out_3[3]));  // open: en
  Adder #(.width(1)) adder_4 (.a(multiplexer_8_out), .b(out_3[3]));  // open: out, cin, cout
  Hex_Digit_Display hex_digit_display_1 (.value(out_3));  // open: dp
  Filtro filtro_1 (.Utente(out_3), .out_2(filtro_1_out_2));
  Multiplexer multiplexer_9 (.in0(filtro_1_out_2), .in1(1'b1), .out(Reset), .sel(Reset_Manuale));  // open: en

  // Other names for the same wires on the sheet: Memoria_1 = out_3[0]; Memoria_2 = out_3[1]; Memoria_3 = out_3[2];
  //   Memoria_4 = out_3[3]

  // Notes on the sheet:
  //   Contenuto dei blocchi di memoria Flip Flop di tipo D
  //   Numero ottenuto dall'unione dei blocchi di memoria
  //   Reset a zero quando N > 9
endmodule

module Serie_non_uguale (
  input  VITTORIA_SCONFITTA,
  input  S1,
  input  S2,
  input  S3,
  input  S4,
  input  S5,
  input  S6,
  input  S7,
  input  S8,
  input  S9,
  input  RESET,
  output PROSSIMO_BLOCCO,
  output SCONFITTA
);

  wire d_ff_1_q, d_ff_1_qn, d_ff_2_qn, multiplexer_1_out, not_1_out, not_2_out, or_1_out;

  or or_1 (or_1_out, S1, S2, S3, S4, S5, S6, S7, S8);
  Multiplexer multiplexer_1 (.in0(1'b0), .in1(1'b1), .out(multiplexer_1_out), .sel(not_1_out));  // open: en
  not not_1 (not_1_out, d_ff_1_q);
  Multiplexer multiplexer_2 (.in0(or_1_out), .in1(1'b0), .out(PROSSIMO_BLOCCO), .sel(VITTORIA_SCONFITTA));  // open: en
  D_Flip_Flop #(.trigger("falling")) d_ff_1 (
    .clk(S9), .D(multiplexer_1_out), .Q(d_ff_1_q), .Qn(d_ff_1_qn), .preset(d_ff_1_qn), .reset(RESET));  // open: en
  not not_2 (not_2_out, d_ff_1_q);
  D_Flip_Flop d_ff_2 (
    .clk(not_2_out), .D(d_ff_2_qn), .Q(SCONFITTA), .Qn(d_ff_2_qn), .reset(RESET));  // open: preset, en
endmodule

module Switch_Posizioni_a_4 (
  input  PULSANTE,
  input  RESET,
  output out_3,
  output out_4,
  output out_5,
  output out_6
);

  wire and_1_out, and_2_out, multiplexer_1_out, multiplexer_2_out, multiplexer_3_out, multiplexer_4_out,
       NAND_4, or_1_out, Vuoto_1, Vuoto_2, Vuoto_3, Vuoto_4;

  Multiplexer multiplexer_1 (.in0(1'b0), .in1(Vuoto_1), .out(multiplexer_1_out), .sel(and_1_out));  // open: en
  Multiplexer multiplexer_2 (.in0(1'b0), .in1(1'b1), .out(multiplexer_2_out), .sel(multiplexer_1_out));  // open: en
  buf or_1 (or_1_out, multiplexer_4_out);  // OR_Gate
  and and_1 (and_1_out, NAND_4, Vuoto_3, Vuoto_2, Vuoto_1);
  D_Flip_Flop d_ff_1 (
    .clk(PULSANTE), .D(multiplexer_2_out), .Q(out_4), .Qn(Vuoto_1), .preset(multiplexer_3_out),
    .reset(or_1_out));  // open: en
  Multiplexer multiplexer_3 (.in0(1'b0), .in1(1'b1), .out(multiplexer_3_out), .sel(and_2_out));  // open: en
  Multiplexer multiplexer_4 (.in0(1'b1), .in1(1'b0), .out(multiplexer_4_out), .sel(and_2_out));  // open: en
  D_Flip_Flop d_ff_2 (.clk(PULSANTE), .D(out_4), .Q(out_5), .Qn(Vuoto_2), .reset(RESET));  // open: preset, en
  and and_2 (and_2_out, Vuoto_4, Vuoto_3, Vuoto_2);
  D_Flip_Flop d_ff_3 (.clk(PULSANTE), .D(out_5), .Q(out_6), .Qn(Vuoto_3), .reset(RESET));  // open: preset, en
  D_Flip_Flop d_ff_4 (.clk(PULSANTE), .D(out_6), .Q(out_3), .Qn(Vuoto_4), .reset(RESET));  // open: preset, en
  nand nand_1 (NAND_4, out_3, Vuoto_4);
endmodule

module Switch_Posizione_a_9 (
  input  PULSANTE,
  input  RESET,
  input  VITTORIA_SCONFITTA,
  output out_4,
  output out_5,
  output out_6,
  output out_7,
  output out_8,
  output out_9,
  output out_10,
  output out_11,
  output out_12
);

  wire and_1_out, and_2_out, d_ff_1_qn, d_ff_2_qn, d_ff_3_qn, d_ff_4_qn, d_ff_5_qn, d_ff_6_qn, d_ff_7_qn,
       d_ff_8_qn, d_ff_9_qn, multiplexer_1_out, multiplexer_2_out, multiplexer_3_out, multiplexer_4_out,
       multiplexer_5_out, nand_1_out;

  Multiplexer multiplexer_1 (.in0(PULSANTE), .out(multiplexer_1_out), .sel(VITTORIA_SCONFITTA));  // open: in1, en
  Multiplexer multiplexer_2 (.in0(1'b0), .in1(d_ff_1_qn), .out(multiplexer_2_out), .sel(and_1_out));  // open: en
  D_Flip_Flop d_ff_1 (
    .clk(multiplexer_1_out), .D(multiplexer_3_out), .Q(out_5), .Qn(d_ff_1_qn), .preset(multiplexer_4_out),
    .reset(multiplexer_5_out));  // open: en
  Multiplexer multiplexer_3 (.in0(1'b0), .in1(1'b1), .out(multiplexer_3_out), .sel(multiplexer_2_out));  // open: en
  Multiplexer multiplexer_4 (.in0(1'b0), .in1(1'b1), .out(multiplexer_4_out), .sel(and_2_out));  // open: en
  Multiplexer multiplexer_5 (.in0(1'b1), .in1(1'b0), .out(multiplexer_5_out), .sel(and_2_out));  // open: en
  D_Flip_Flop d_ff_2 (
    .clk(multiplexer_1_out), .D(out_5), .Q(out_6), .Qn(d_ff_2_qn), .reset(RESET));  // open: preset, en
  D_Flip_Flop d_ff_3 (
    .clk(multiplexer_1_out), .D(out_6), .Q(out_7), .Qn(d_ff_3_qn), .reset(RESET));  // open: preset, en
  and and_1 (and_1_out, d_ff_1_qn, d_ff_2_qn, d_ff_3_qn, d_ff_4_qn, d_ff_5_qn, d_ff_6_qn, d_ff_7_qn, d_ff_8_qn, nand_1_out);
  D_Flip_Flop d_ff_4 (
    .clk(multiplexer_1_out), .D(out_7), .Q(out_8), .Qn(d_ff_4_qn), .reset(RESET));  // open: preset, en
  and and_2 (and_2_out, d_ff_2_qn, d_ff_3_qn, d_ff_4_qn, d_ff_5_qn, d_ff_6_qn, d_ff_7_qn, d_ff_8_qn, d_ff_9_qn);
  D_Flip_Flop d_ff_5 (
    .clk(multiplexer_1_out), .D(out_8), .Q(out_9), .Qn(d_ff_5_qn), .reset(RESET));  // open: preset, en
  D_Flip_Flop d_ff_6 (
    .clk(multiplexer_1_out), .D(out_9), .Q(out_10), .Qn(d_ff_6_qn), .reset(RESET));  // open: preset, en
  D_Flip_Flop d_ff_7 (
    .clk(multiplexer_1_out), .D(out_10), .Q(out_11), .Qn(d_ff_7_qn), .reset(RESET));  // open: preset, en
  D_Flip_Flop d_ff_8 (
    .clk(multiplexer_1_out), .D(out_11), .Q(out_12), .Qn(d_ff_8_qn), .reset(RESET));  // open: preset, en
  D_Flip_Flop d_ff_9 (
    .clk(multiplexer_1_out), .D(out_12), .Q(out_4), .Qn(d_ff_9_qn), .reset(RESET));  // open: preset, en
  nand nand_1 (nand_1_out, out_4, d_ff_9_qn);
endmodule

module Nascondi_Codice_Codificatore (
  input  [3:0] in_1,
  input  Pulsante,
  input  [3:0] in_3,
  input  [3:0] in_4,
  input  [3:0] in_5,
  output [3:0] out_6,
  output [3:0] out_7,
  output [3:0] out_8,
  output [3:0] out_9
);

  wire d_ff_1_q, multiplexer_1_out, not_1_out;

  Multiplexer multiplexer_1 (.in0(1'b0), .in1(1'b1), .out(multiplexer_1_out), .sel(not_1_out));  // open: en
  not not_1 (not_1_out, d_ff_1_q);
  D_Flip_Flop d_ff_1 (.clk(Pulsante), .D(multiplexer_1_out), .Q(d_ff_1_q));  // open: Qn, preset, en, reset
  Multiplexer #(.width(4)) multiplexer_2 (.in0(in_1), .out(out_6), .sel(d_ff_1_q));  // open: in1, en
  Multiplexer #(.width(4)) multiplexer_3 (.in0(in_3), .out(out_7), .sel(d_ff_1_q));  // open: in1, en
  Multiplexer #(.width(4)) multiplexer_4 (.in0(in_4), .out(out_8), .sel(d_ff_1_q));  // open: in1, en
  Multiplexer #(.width(4)) multiplexer_5 (.in0(in_5), .out(out_9), .sel(d_ff_1_q));  // open: in1, en
endmodule

module Nascondi_Codice_Decodificatore (
  input  Pulsante,
  input  [3:0] in_2,
  input  RESET,
  input  [3:0] in_4,
  input  [3:0] in_5,
  input  [3:0] in_6,
  output [3:0] out_7,
  output [3:0] out_8,
  output [3:0] out_9,
  output [3:0] out_10
);

  wire d_ff_1_q;

  D_Flip_Flop d_ff_1 (.Q(d_ff_1_q), .preset(Pulsante), .reset(RESET));  // open: clk, D, Qn, en
  Multiplexer #(.width(4)) multiplexer_1 (.in1(in_2), .out(out_7), .sel(d_ff_1_q));  // open: in0, en
  Multiplexer #(.width(4)) multiplexer_2 (.in1(in_4), .out(out_8), .sel(d_ff_1_q));  // open: in0, en
  Multiplexer #(.width(4)) multiplexer_3 (.in1(in_5), .out(out_9), .sel(d_ff_1_q));  // open: in0, en
  Multiplexer #(.width(4)) multiplexer_4 (.in1(in_6), .out(out_10), .sel(d_ff_1_q));  // open: in0, en
endmodule

module Salva_Scelta_Codificatore (
  input  Reset,
  input  Pulsante,
  input  [3:0] in_3,
  input  [3:0] in_4,
  input  [3:0] in_5,
  input  [3:0] in_6,
  output [3:0] out_7,
  output [3:0] out_8,
  output [3:0] out_9,
  output [3:0] out_10
);

  wire d_ff_1_qn, d_ff_2_q, d_ff_3_q, d_ff_4_q, d_ff_5_q, multiplexer_1_out, multiplexer_2_out,
       multiplexer_3_out, multiplexer_4_out, or_1_out, or_2_out, or_3_out, or_4_out;
  wire [3:0] d_ff_18_q, d_ff_19_q, d_ff_20_q, d_ff_21_q, multiplexer_6_out, multiplexer_8_out,
       multiplexer_10_out, multiplexer_12_out, multiplexer_13_out, multiplexer_14_out, multiplexer_15_out,
       multiplexer_16_out;

  D_Flip_Flop d_ff_1 (.Qn(d_ff_1_qn), .preset(Pulsante), .reset(Reset));  // open: clk, D, Q, en
  Multiplexer multiplexer_1 (.in0(1'b0), .in1(1'b1), .out(multiplexer_1_out), .sel(or_1_out));  // open: en
  Multiplexer multiplexer_2 (.in0(1'b0), .in1(1'b1), .out(multiplexer_2_out), .sel(or_2_out));  // open: en
  Multiplexer multiplexer_3 (.in0(1'b0), .in1(1'b1), .out(multiplexer_3_out), .sel(or_3_out));  // open: en
  Multiplexer multiplexer_4 (.in0(1'b0), .in1(1'b1), .out(multiplexer_4_out), .sel(or_4_out));  // open: en
  D_Flip_Flop d_ff_2 (.clk(Pulsante), .D(multiplexer_1_out), .Q(d_ff_2_q), .reset(Reset));  // open: Qn, preset, en
  or or_1 (or_1_out, d_ff_2_q, d_ff_1_qn);
  D_Flip_Flop d_ff_3 (.clk(Pulsante), .D(multiplexer_2_out), .Q(d_ff_3_q), .reset(Reset));  // open: Qn, preset, en
  or or_2 (or_2_out, d_ff_3_q, d_ff_1_qn);
  D_Flip_Flop d_ff_4 (.clk(Pulsante), .D(multiplexer_3_out), .Q(d_ff_4_q), .reset(Reset));  // open: Qn, preset, en
  or or_3 (or_3_out, d_ff_4_q, d_ff_1_qn);
  D_Flip_Flop d_ff_5 (.clk(Pulsante), .D(multiplexer_4_out), .Q(d_ff_5_q), .reset(Reset));  // open: Qn, preset, en
  or or_4 (or_4_out, d_ff_5_q, d_ff_1_qn);
  Multiplexer #(.width(4)) multiplexer_5 (.in0(in_3), .in1(d_ff_18_q), .out(out_7), .sel(d_ff_2_q));  // open: en
  Multiplexer #(.width(4)) multiplexer_6 (
    .in0(in_3), .in1(4'b0000), .out(multiplexer_6_out), .sel(d_ff_2_q));  // open: en
  Multiplexer #(.width(4)) multiplexer_7 (.in0(in_4), .in1(d_ff_19_q), .out(out_8), .sel(d_ff_3_q));  // open: en
  Multiplexer #(.width(4)) multiplexer_8 (
    .in0(in_4), .in1(4'b0000), .out(multiplexer_8_out), .sel(d_ff_3_q));  // open: en
  Multiplexer #(.width(4)) multiplexer_9 (.in0(in_5), .in1(d_ff_20_q), .out(out_9), .sel(d_ff_4_q));  // open: en
  Multiplexer #(.width(4)) multiplexer_10 (
    .in0(in_5), .in1(4'b0000), .out(multiplexer_10_out), .sel(d_ff_4_q));  // open: en
  Multiplexer #(.width(4)) multiplexer_11 (.in0(in_6), .in1(d_ff_21_q), .out(out_10), .sel(d_ff_5_q));  // open: en
  Multiplexer #(.width(4)) multiplexer_12 (
    .in0(in_6), .in1(4'b0000), .out(multiplexer_12_out), .sel(d_ff_5_q));  // open: en
  Multiplexer #(.width(4)) multiplexer_13 (
    .in0(d_ff_18_q), .in1(multiplexer_6_out), .out(multiplexer_13_out), .sel(Pulsante));  // open: en
  Multiplexer #(.width(4)) multiplexer_14 (
    .in0(d_ff_19_q), .in1(multiplexer_8_out), .out(multiplexer_14_out), .sel(Pulsante));  // open: en
  Multiplexer #(.width(4)) multiplexer_15 (
    .in0(d_ff_20_q), .in1(multiplexer_10_out), .out(multiplexer_15_out), .sel(Pulsante));  // open: en
  Multiplexer #(.width(4)) multiplexer_16 (
    .in0(d_ff_21_q), .in1(multiplexer_12_out), .out(multiplexer_16_out), .sel(Pulsante));  // open: en
  D_Flip_Flop d_ff_6 (.Q(d_ff_18_q[3]), .preset(multiplexer_13_out[3]), .reset(Reset));  // open: clk, D, Qn, en
  D_Flip_Flop d_ff_7 (.Q(d_ff_18_q[2]), .preset(multiplexer_13_out[2]), .reset(Reset));  // open: clk, D, Qn, en
  D_Flip_Flop d_ff_8 (.Q(d_ff_19_q[3]), .preset(multiplexer_14_out[3]), .reset(Reset));  // open: clk, D, Qn, en
  D_Flip_Flop d_ff_9 (.Q(d_ff_19_q[2]), .preset(multiplexer_14_out[2]), .reset(Reset));  // open: clk, D, Qn, en
  D_Flip_Flop d_ff_10 (.Q(d_ff_20_q[2]), .preset(multiplexer_15_out[2]), .reset(Reset));  // open: clk, D, Qn, en
  D_Flip_Flop d_ff_11 (.Q(d_ff_20_q[3]), .preset(multiplexer_15_out[3]), .reset(Reset));  // open: clk, D, Qn, en
  D_Flip_Flop d_ff_12 (.Q(d_ff_21_q[3]), .preset(multiplexer_16_out[3]), .reset(Reset));  // open: clk, D, Qn, en
  D_Flip_Flop d_ff_13 (.Q(d_ff_21_q[2]), .preset(multiplexer_16_out[2]), .reset(Reset));  // open: clk, D, Qn, en
  D_Flip_Flop d_ff_14 (.Q(d_ff_18_q[1]), .preset(multiplexer_13_out[1]), .reset(Reset));  // open: clk, D, Qn, en
  D_Flip_Flop d_ff_15 (.Q(d_ff_19_q[1]), .preset(multiplexer_14_out[1]), .reset(Reset));  // open: clk, D, Qn, en
  D_Flip_Flop d_ff_16 (.Q(d_ff_20_q[1]), .preset(multiplexer_15_out[1]), .reset(Reset));  // open: clk, D, Qn, en
  D_Flip_Flop d_ff_17 (.Q(d_ff_21_q[1]), .preset(multiplexer_16_out[1]), .reset(Reset));  // open: clk, D, Qn, en
  D_Flip_Flop d_ff_18 (.Q(d_ff_18_q[0]), .preset(multiplexer_13_out[0]), .reset(Reset));  // open: clk, D, Qn, en
  D_Flip_Flop d_ff_19 (.Q(d_ff_19_q[0]), .preset(multiplexer_14_out[0]), .reset(Reset));  // open: clk, D, Qn, en
  D_Flip_Flop d_ff_20 (.Q(d_ff_20_q[0]), .preset(multiplexer_15_out[0]), .reset(Reset));  // open: clk, D, Qn, en
  D_Flip_Flop d_ff_21 (.Q(d_ff_21_q[0]), .preset(multiplexer_16_out[0]), .reset(Reset));  // open: clk, D, Qn, en

  // Other names for the same wires on the sheet: R = Reset
endmodule

module Salva_Scelta_Decodificatore (
  input  Reset,
  input  Pulsante,
  input  [3:0] in_3,
  input  [3:0] in_4,
  input  [3:0] in_5,
  input  [3:0] in_6,
  output [3:0] out_7,
  output [3:0] out_8,
  output [3:0] out_9,
  output [3:0] out_10
);

  wire d_ff_1_qn, d_ff_2_q, d_ff_3_q, d_ff_4_q, d_ff_5_q, d_ff_13_qn, multiplexer_1_out, multiplexer_2_out,
       multiplexer_3_out, multiplexer_4_out, or_1_out, or_2_out, or_3_out, or_4_out;
  wire [3:0] d_ff_18_q, d_ff_19_q, d_ff_20_q, d_ff_21_q, multiplexer_6_out, multiplexer_8_out,
       multiplexer_10_out, multiplexer_12_out, multiplexer_13_out, multiplexer_14_out, multiplexer_15_out,
       multiplexer_16_out;

  D_Flip_Flop d_ff_1 (.Qn(d_ff_1_qn), .preset(Pulsante), .reset(Reset));  // open: clk, D, Q, en
  Multiplexer multiplexer_1 (.in0(1'b0), .in1(1'b1), .out(multiplexer_1_out), .sel(or_1_out));  // open: en
  Multiplexer multiplexer_2 (.in0(1'b0), .in1(1'b1), .out(multiplexer_2_out), .sel(or_2_out));  // open: en
  Multiplexer multiplexer_3 (.in0(1'b0), .in1(1'b1), .out(multiplexer_3_out), .sel(or_3_out));  // open: en
  Multiplexer multiplexer_4 (.in0(1'b0), .in1(1'b1), .out(multiplexer_4_out), .sel(or_4_out));  // open: en
  D_Flip_Flop d_ff_2 (.clk(Pulsante), .D(multiplexer_1_out), .Q(d_ff_2_q), .reset(Reset));  // open: Qn, preset, en
  or or_1 (or_1_out, d_ff_2_q, d_ff_1_qn);
  D_Flip_Flop d_ff_3 (.clk(Pulsante), .D(multiplexer_2_out), .Q(d_ff_3_q), .reset(Reset));  // open: Qn, preset, en
  or or_2 (or_2_out, d_ff_3_q, d_ff_1_qn);
  D_Flip_Flop d_ff_4 (.clk(Pulsante), .D(multiplexer_3_out), .Q(d_ff_4_q), .reset(Reset));  // open: Qn, preset, en
  or or_3 (or_3_out, d_ff_4_q, d_ff_1_qn);
  D_Flip_Flop d_ff_5 (.clk(Pulsante), .D(multiplexer_4_out), .Q(d_ff_5_q), .reset(Reset));  // open: Qn, preset, en
  or or_4 (or_4_out, d_ff_5_q, d_ff_1_qn);
  Multiplexer #(.width(4)) multiplexer_5 (.in0(in_3), .in1(d_ff_18_q), .out(out_7), .sel(d_ff_2_q));  // open: en
  Multiplexer #(.width(4)) multiplexer_6 (
    .in0(in_3), .in1(4'b0000), .out(multiplexer_6_out), .sel(d_ff_2_q));  // open: en
  Multiplexer #(.width(4)) multiplexer_7 (.in0(in_4), .in1(d_ff_19_q), .out(out_8), .sel(d_ff_3_q));  // open: en
  Multiplexer #(.width(4)) multiplexer_8 (
    .in0(in_4), .in1(4'b0000), .out(multiplexer_8_out), .sel(d_ff_3_q));  // open: en
  Multiplexer #(.width(4)) multiplexer_9 (.in0(in_5), .in1(d_ff_20_q), .out(out_9), .sel(d_ff_4_q));  // open: en
  Multiplexer #(.width(4)) multiplexer_10 (
    .in0(in_5), .in1(4'b0000), .out(multiplexer_10_out), .sel(d_ff_4_q));  // open: en
  Multiplexer #(.width(4)) multiplexer_11 (.in0(in_6), .in1(d_ff_21_q), .out(out_10), .sel(d_ff_5_q));  // open: en
  Multiplexer #(.width(4)) multiplexer_12 (
    .in0(in_6), .in1(4'b0000), .out(multiplexer_12_out), .sel(d_ff_5_q));  // open: en
  Multiplexer #(.width(4)) multiplexer_13 (
    .in0(d_ff_18_q), .in1(multiplexer_6_out), .out(multiplexer_13_out), .sel(Pulsante));  // open: en
  Multiplexer #(.width(4)) multiplexer_14 (
    .in0(d_ff_19_q), .in1(multiplexer_8_out), .out(multiplexer_14_out), .sel(Pulsante));  // open: en
  Multiplexer #(.width(4)) multiplexer_15 (
    .in0(d_ff_20_q), .in1(multiplexer_10_out), .out(multiplexer_15_out), .sel(Pulsante));  // open: en
  Multiplexer #(.width(4)) multiplexer_16 (
    .in0(d_ff_21_q), .in1(multiplexer_12_out), .out(multiplexer_16_out), .sel(Pulsante));  // open: en
  D_Flip_Flop d_ff_6 (.Q(d_ff_18_q[3]), .preset(multiplexer_13_out[3]), .reset(Reset));  // open: clk, D, Qn, en
  D_Flip_Flop d_ff_7 (.Q(d_ff_18_q[2]), .preset(multiplexer_13_out[2]), .reset(Reset));  // open: clk, D, Qn, en
  D_Flip_Flop d_ff_8 (.Q(d_ff_19_q[2]), .preset(multiplexer_14_out[2]), .reset(Reset));  // open: clk, D, Qn, en
  D_Flip_Flop d_ff_9 (.Q(d_ff_19_q[3]), .preset(multiplexer_14_out[3]), .reset(Reset));  // open: clk, D, Qn, en
  D_Flip_Flop d_ff_10 (.Q(d_ff_20_q[2]), .preset(multiplexer_15_out[2]), .reset(Reset));  // open: clk, D, Qn, en
  D_Flip_Flop d_ff_11 (.Q(d_ff_20_q[3]), .preset(multiplexer_15_out[3]), .reset(Reset));  // open: clk, D, Qn, en
  D_Flip_Flop d_ff_12 (.Q(d_ff_21_q[2]), .preset(multiplexer_16_out[2]), .reset(Reset));  // open: clk, D, Qn, en
  D_Flip_Flop d_ff_13 (
    .Q(d_ff_21_q[3]), .Qn(d_ff_13_qn), .preset(multiplexer_16_out[3]), .reset(Reset));  // open: clk, D, en
  D_Flip_Flop d_ff_14 (.Q(d_ff_18_q[1]), .preset(multiplexer_13_out[1]), .reset(Reset));  // open: clk, D, Qn, en
  D_Flip_Flop d_ff_15 (.Q(d_ff_19_q[1]), .preset(multiplexer_14_out[1]), .reset(Reset));  // open: clk, D, Qn, en
  D_Flip_Flop d_ff_16 (.Q(d_ff_20_q[1]), .preset(multiplexer_15_out[1]), .reset(Reset));  // open: clk, D, Qn, en
  D_Flip_Flop d_ff_17 (.Q(d_ff_21_q[1]), .preset(multiplexer_16_out[1]), .reset(Reset));  // open: clk, D, Qn, en
  D_Flip_Flop d_ff_18 (.Q(d_ff_18_q[0]), .preset(multiplexer_13_out[0]), .reset(Reset));  // open: clk, D, Qn, en
  D_Flip_Flop d_ff_19 (.Q(d_ff_19_q[0]), .preset(multiplexer_14_out[0]), .reset(Reset));  // open: clk, D, Qn, en
  D_Flip_Flop d_ff_20 (.Q(d_ff_20_q[0]), .preset(multiplexer_15_out[0]), .reset(Reset));  // open: clk, D, Qn, en
  D_Flip_Flop d_ff_21 (.Q(d_ff_21_q[0]), .preset(multiplexer_16_out[0]), .reset(Reset));  // open: clk, D, Qn, en

  // Other names for the same wires on the sheet: R = Reset
endmodule

module Confronto_N_1 (
  input  [3:0] Decodificatore,
  input  [3:0] Codice_4,
  input  [3:0] Codice_1,
  input  [3:0] Codice_2,
  input  [3:0] Codice_3,
  output Verde___Posto_giusto,
  output Rosso___Numero_giusto___Posto_sbagliato
);

  wire _2, _3, _4, multiplexer_1_out, or_1_out;

  Comparator #(.width(4)) comparator_1 (.a(Decodificatore), .b(Codice_4), .eq(Verde___Posto_giusto));  // open: gt, lt
  or or_1 (or_1_out, _2, _3, _4);
  LED led_1 (.in(Verde___Posto_giusto));
  LED led_2 (.in(Rosso___Numero_giusto___Posto_sbagliato));
  and and_1 (Rosso___Numero_giusto___Posto_sbagliato, ~Verde___Posto_giusto, multiplexer_1_out);  // AND_Gate
  Multiplexer multiplexer_1 (
    .in0(or_1_out), .in1(1'b0), .out(multiplexer_1_out), .sel(Verde___Posto_giusto));  // open: en
  Comparator #(.width(4)) comparator_2 (.a(Decodificatore), .b(Codice_1), .eq(_2));  // open: gt, lt
  Comparator #(.width(4)) comparator_3 (.a(Decodificatore), .b(Codice_2), .eq(_3));  // open: gt, lt
  Comparator #(.width(4)) comparator_4 (.a(Decodificatore), .b(Codice_3), .eq(_4));  // open: gt, lt

  // Other names for the same wires on the sheet: _1 = Verde___Posto_giusto
endmodule

module Confronto_N_2 (
  input  [3:0] Decodificatore,
  input  [3:0] Codice_4,
  input  [3:0] Codice_1,
  input  [3:0] Codice_2,
  input  [3:0] Codice_3,
  output Verde___Posto_giusto,
  output Rosso___Numero_giusto___Posto_sbagliato
);

  wire _1, _3, _4, multiplexer_1_out, or_1_out;

  Comparator #(.width(4)) comparator_1 (.a(Decodificatore), .b(Codice_4), .eq(_1));  // open: gt, lt
  or or_1 (or_1_out, _3, _4, _1);
  LED led_1 (.in(Verde___Posto_giusto));
  LED led_2 (.in(Rosso___Numero_giusto___Posto_sbagliato));
  and and_1 (Rosso___Numero_giusto___Posto_sbagliato, ~Verde___Posto_giusto, multiplexer_1_out);  // AND_Gate
  Multiplexer multiplexer_1 (
    .in0(or_1_out), .in1(1'b0), .out(multiplexer_1_out), .sel(Verde___Posto_giusto));  // open: en
  Comparator #(.width(4)) comparator_2 (.a(Decodificatore), .b(Codice_1), .eq(Verde___Posto_giusto));  // open: gt, lt
  Comparator #(.width(4)) comparator_3 (.a(Decodificatore), .b(Codice_2), .eq(_3));  // open: gt, lt
  Comparator #(.width(4)) comparator_4 (.a(Decodificatore), .b(Codice_3), .eq(_4));  // open: gt, lt

  // Other names for the same wires on the sheet: _2 = Verde___Posto_giusto
endmodule

module Confronto_N_3 (
  input  [3:0] Decodificatore,
  input  [3:0] Codice_4,
  input  [3:0] Codice_1,
  input  [3:0] Codice_2,
  input  [3:0] Codice_3,
  output Verde___Posto_giusto,
  output Rosso___Numero_giusto___Posto_sbagliato
);

  wire _1, _2, _4, multiplexer_1_out, or_1_out;

  Comparator #(.width(4)) comparator_1 (.a(Decodificatore), .b(Codice_4), .eq(_1));  // open: gt, lt
  or or_1 (or_1_out, _4, _1, _2);
  LED led_1 (.in(Verde___Posto_giusto));
  LED led_2 (.in(Rosso___Numero_giusto___Posto_sbagliato));
  and and_1 (Rosso___Numero_giusto___Posto_sbagliato, ~Verde___Posto_giusto, multiplexer_1_out);  // AND_Gate
  Multiplexer multiplexer_1 (
    .in0(or_1_out), .in1(1'b0), .out(multiplexer_1_out), .sel(Verde___Posto_giusto));  // open: en
  Comparator #(.width(4)) comparator_2 (.a(Decodificatore), .b(Codice_1), .eq(_2));  // open: gt, lt
  Comparator #(.width(4)) comparator_3 (.a(Decodificatore), .b(Codice_2), .eq(Verde___Posto_giusto));  // open: gt, lt
  Comparator #(.width(4)) comparator_4 (.a(Decodificatore), .b(Codice_3), .eq(_4));  // open: gt, lt

  // Other names for the same wires on the sheet: _3 = Verde___Posto_giusto
endmodule

module Confronto_N_4 (
  input  [3:0] Decodificatore,
  input  [3:0] Codice_4,
  input  [3:0] Codice_1,
  input  [3:0] Codice_2,
  input  [3:0] Codice_3,
  output Verde___Posto_giusto,
  output Rosso___Numero_giusto___Posto_sbagliato
);

  wire _1, _2, _3, multiplexer_1_out, or_1_out;

  Comparator #(.width(4)) comparator_1 (.a(Decodificatore), .b(Codice_4), .eq(_1));  // open: gt, lt
  or or_1 (or_1_out, _1, _2, _3);
  LED led_1 (.in(Verde___Posto_giusto));
  LED led_2 (.in(Rosso___Numero_giusto___Posto_sbagliato));
  and and_1 (Rosso___Numero_giusto___Posto_sbagliato, ~Verde___Posto_giusto, multiplexer_1_out);  // AND_Gate
  Multiplexer multiplexer_1 (
    .in0(or_1_out), .in1(1'b0), .out(multiplexer_1_out), .sel(Verde___Posto_giusto));  // open: en
  Comparator #(.width(4)) comparator_2 (.a(Decodificatore), .b(Codice_1), .eq(_2));  // open: gt, lt
  Comparator #(.width(4)) comparator_3 (.a(Decodificatore), .b(Codice_2), .eq(_3));  // open: gt, lt
  Comparator #(.width(4)) comparator_4 (.a(Decodificatore), .b(Codice_3), .eq(Verde___Posto_giusto));  // open: gt, lt

  // Other names for the same wires on the sheet: _4 = Verde___Posto_giusto
endmodule

module Risultato_Confronto (
  input  [3:0] in_1,
  input  [3:0] in_2,
  input  [3:0] in_3,
  input  [3:0] in_4,
  input  RESET,
  input  [3:0] in_6,
  input  [3:0] in_7,
  input  [3:0] in_8,
  input  [3:0] in_9,
  input  PULSANTE,
  output VERDE_1,
  output VERDE_2,
  output VERDE_3,
  output VERDE_4,
  output ROSSO_4,
  output ROSSO_3,
  output ROSSO_2,
  output ROSSO_1,
  output VITTORIA,
  output PROSSIMI_SLOT
);

  wire confronto_n_1_1_rosso___numero_giusto___posto_sbagliato, confronto_n_1_1_verde___posto_giusto,
       confronto_n_2_1_rosso___numero_giusto___posto_sbagliato, confronto_n_2_1_verde___posto_giusto,
       confronto_n_3_1_rosso___numero_giusto___posto_sbagliato, confronto_n_3_1_verde___posto_giusto,
       confronto_n_4_1_rosso___numero_giusto___posto_sbagliato, confronto_n_4_1_verde___posto_giusto,
       d_ff_1_q, d_ff_1_qn, d_ff_2_q, d_ff_2_qn, multiplexer_4_out, multiplexer_6_out, multiplexer_7_out,
       multiplexer_8_out, multiplexer_9_out, multiplexer_10_out, multiplexer_11_out, multiplexer_12_out,
       multiplexer_13_out, not_1_out, ROSSO_1_t, ROSSO_2_t, ROSSO_3_t, ROSSO_4_t, VERDE_1_t, VERDE_2_t,
       VERDE_3_t, VERDE_4_t;
  wire [3:0] blocco_per_risultato_confronto_1_out_11, blocco_per_risultato_confronto_1_out_12,
       blocco_per_risultato_confronto_1_out_13, blocco_per_risultato_confronto_1_out_14, multiplexer_1_out,
       multiplexer_2_out, multiplexer_3_out, multiplexer_5_out;

  Blocco_per__Risultato_Confronto blocco_per_risultato_confronto_1 (
    .in_1(in_1), .in_2(in_6), .in_3(in_2), .in_4(in_7), .in_6(in_3), .in_7(in_8), .in_8(in_4), .in_9(in_9),
    .out_12(blocco_per_risultato_confronto_1_out_12), .out_13(blocco_per_risultato_confronto_1_out_13),
    .out_14(blocco_per_risultato_confronto_1_out_14), .PULSANTE(PULSANTE),
    .out_11(blocco_per_risultato_confronto_1_out_11), .RESET(RESET));
  Multiplexer #(.width(4)) multiplexer_1 (.in0(in_2), .out(multiplexer_1_out), .sel(d_ff_2_q));  // open: in1, en
  Multiplexer #(.width(4)) multiplexer_2 (.in0(in_3), .out(multiplexer_2_out), .sel(d_ff_2_q));  // open: in1, en
  Multiplexer #(.width(4)) multiplexer_3 (.in0(in_4), .out(multiplexer_3_out), .sel(d_ff_2_q));  // open: in1, en
  Multiplexer multiplexer_4 (.in0(1'b0), .in1(1'b1), .out(multiplexer_4_out), .sel(not_1_out));  // open: en
  not not_1 (not_1_out, d_ff_1_q);
  Multiplexer #(.width(4)) multiplexer_5 (.in0(in_1), .out(multiplexer_5_out), .sel(d_ff_2_q));  // open: in1, en
  D_Flip_Flop #(.trigger("falling")) d_ff_1 (
    .clk(PULSANTE), .D(multiplexer_4_out), .Q(d_ff_1_q), .Qn(d_ff_1_qn), .preset(d_ff_1_qn));  // open: en, reset
  D_Flip_Flop d_ff_2 (.clk(d_ff_1_qn), .D(d_ff_2_qn), .Q(d_ff_2_q), .Qn(d_ff_2_qn), .reset(RESET));  // open: preset, en
  Confronto_N_1 confronto_n_1_1 (
    .Decodificatore(blocco_per_risultato_confronto_1_out_11), .Codice_4(multiplexer_5_out),
    .Codice_1(multiplexer_1_out), .Codice_2(multiplexer_2_out), .Codice_3(multiplexer_3_out),
    .Verde___Posto_giusto(confronto_n_1_1_verde___posto_giusto),
    .Rosso___Numero_giusto___Posto_sbagliato(confronto_n_1_1_rosso___numero_giusto___posto_sbagliato));
  Confronto_N_2 confronto_n_2_1 (
    .Decodificatore(blocco_per_risultato_confronto_1_out_12), .Codice_4(multiplexer_5_out),
    .Codice_1(multiplexer_1_out), .Codice_2(multiplexer_2_out), .Codice_3(multiplexer_3_out),
    .Verde___Posto_giusto(confronto_n_2_1_verde___posto_giusto),
    .Rosso___Numero_giusto___Posto_sbagliato(confronto_n_2_1_rosso___numero_giusto___posto_sbagliato));
  Confronto_N_3 confronto_n_3_1 (
    .Decodificatore(blocco_per_risultato_confronto_1_out_13), .Codice_4(multiplexer_5_out),
    .Codice_1(multiplexer_1_out), .Codice_2(multiplexer_2_out), .Codice_3(multiplexer_3_out),
    .Verde___Posto_giusto(confronto_n_3_1_verde___posto_giusto),
    .Rosso___Numero_giusto___Posto_sbagliato(confronto_n_3_1_rosso___numero_giusto___posto_sbagliato));
  Confronto_N_4 confronto_n_4_1 (
    .Decodificatore(blocco_per_risultato_confronto_1_out_14), .Codice_4(multiplexer_5_out),
    .Codice_1(multiplexer_1_out), .Codice_2(multiplexer_2_out), .Codice_3(multiplexer_3_out),
    .Verde___Posto_giusto(confronto_n_4_1_verde___posto_giusto),
    .Rosso___Numero_giusto___Posto_sbagliato(confronto_n_4_1_rosso___numero_giusto___posto_sbagliato));
  Multiplexer multiplexer_6 (
    .in0(1'b0), .in1(confronto_n_1_1_verde___posto_giusto), .out(multiplexer_6_out), .sel(d_ff_1_qn));  // open: en
  Multiplexer multiplexer_7 (
    .in0(1'b0), .in1(confronto_n_1_1_rosso___numero_giusto___posto_sbagliato), .out(multiplexer_7_out),
    .sel(d_ff_1_qn));  // open: en
  Multiplexer multiplexer_8 (
    .in0(1'b0), .in1(confronto_n_2_1_verde___posto_giusto), .out(multiplexer_8_out), .sel(d_ff_1_qn));  // open: en
  Multiplexer multiplexer_9 (
    .in0(1'b0), .in1(confronto_n_2_1_rosso___numero_giusto___posto_sbagliato), .out(multiplexer_9_out),
    .sel(d_ff_1_qn));  // open: en
  Multiplexer multiplexer_10 (
    .in0(1'b0), .in1(confronto_n_3_1_verde___posto_giusto), .out(multiplexer_10_out), .sel(d_ff_1_qn));  // open: en
  Multiplexer multiplexer_11 (
    .in0(1'b0), .in1(confronto_n_3_1_rosso___numero_giusto___posto_sbagliato), .out(multiplexer_11_out),
    .sel(d_ff_1_qn));  // open: en
  Multiplexer multiplexer_12 (
    .in0(1'b0), .in1(confronto_n_4_1_verde___posto_giusto), .out(multiplexer_12_out), .sel(d_ff_1_qn));  // open: en
  Multiplexer multiplexer_13 (
    .in0(1'b0), .in1(confronto_n_4_1_rosso___numero_giusto___posto_sbagliato), .out(multiplexer_13_out),
    .sel(d_ff_1_qn));  // open: en
  D_Flip_Flop d_ff_3 (.Q(VERDE_1_t), .preset(multiplexer_6_out), .reset(RESET));  // open: clk, D, Qn, en
  D_Flip_Flop d_ff_4 (.Q(VERDE_2_t), .preset(multiplexer_8_out), .reset(RESET));  // open: clk, D, Qn, en
  D_Flip_Flop d_ff_5 (.Q(VERDE_3_t), .preset(multiplexer_10_out), .reset(RESET));  // open: clk, D, Qn, en
  D_Flip_Flop d_ff_6 (.Q(VERDE_4_t), .preset(multiplexer_12_out), .reset(RESET));  // open: clk, D, Qn, en
  D_Flip_Flop d_ff_7 (.Q(ROSSO_1_t), .preset(multiplexer_7_out), .reset(RESET));  // open: clk, D, Qn, en
  D_Flip_Flop d_ff_8 (.Q(ROSSO_2_t), .preset(multiplexer_9_out), .reset(RESET));  // open: clk, D, Qn, en
  D_Flip_Flop d_ff_9 (.Q(ROSSO_3_t), .preset(multiplexer_11_out), .reset(RESET));  // open: clk, D, Qn, en
  D_Flip_Flop d_ff_10 (.Q(ROSSO_4_t), .preset(multiplexer_13_out), .reset(RESET));  // open: clk, D, Qn, en
  and and_1 (VITTORIA, VERDE_1_t, VERDE_2_t, VERDE_3_t, VERDE_4_t);
  and and_2 (PROSSIMI_SLOT, ~VITTORIA, d_ff_1_qn);  // AND_Gate
  Luci luci_1 (
    .VERDE_1(VERDE_1_t), .VERDE_2(VERDE_2_t), .VERDE_3(VERDE_3_t), .VERDE_4(VERDE_4_t), .ROSSO_1(ROSSO_1_t),
    .ROSSO_2(ROSSO_2_t), .ROSSO_3(ROSSO_3_t), .ROSSO_4(ROSSO_4_t), .RESET(RESET), .V1(VERDE_1), .R1(ROSSO_4),
    .V2(VERDE_2), .R2(ROSSO_3), .V3(VERDE_3), .R3(ROSSO_2), .V4(VERDE_4), .R4(ROSSO_1));

  // Notes on the sheet:
  //   I numeri del codificatore
  //   Per attivare il confronto e vedere il risultato
endmodule

module Blocco_per__Risultato_Confronto (
  input  [3:0] in_1,
  input  [3:0] in_2,
  input  [3:0] in_3,
  input  [3:0] in_4,
  input  RESET,
  input  [3:0] in_6,
  input  [3:0] in_7,
  input  [3:0] in_8,
  input  [3:0] in_9,
  input  PULSANTE,
  output [3:0] out_11,
  output [3:0] out_12,
  output [3:0] out_13,
  output [3:0] out_14
);

  wire and_2_out, and_3_out, and_4_out, and_12_out, and_13_out, and_14_out, and_16_out, and_17_out,
       and_18_out, C1_D1, C1_D2, C1_D3, C1_D4, C2_D1, C2_D2, C2_D3, C2_D4, C3_D1, C3_D2, C3_D3, C3_D4, C4_D1,
       C4_D2, C4_D3, C4_D4, comparator_1_eq, comparator_2_eq, comparator_3_eq, comparator_4_eq,
       comparator_6_eq, comparator_7_eq, comparator_8_eq, comparator_9_eq, comparator_10_eq,
       comparator_11_eq, comparator_12_eq, comparator_13_eq, comparator_14_eq, comparator_15_eq,
       comparator_16_eq, or_2_out, or_4_out, or_6_out, or_8_out;
  wire [3:0] C1, C2, C3, C4, D1, D2, D3, D4, multiplexer_1_out, multiplexer_2_out, multiplexer_3_out,
       multiplexer_4_out, multiplexer_5_out, multiplexer_6_out, multiplexer_7_out, multiplexer_8_out,
       multiplexer_9_out, multiplexer_10_out, multiplexer_11_out, multiplexer_12_out, multiplexer_13_out,
       multiplexer_14_out, multiplexer_15_out, multiplexer_16_out, multiplexer_17_out, multiplexer_18_out,
       multiplexer_19_out, multiplexer_20_out, multiplexer_25_out, multiplexer_26_out, multiplexer_27_out,
       multiplexer_28_out, or_1_out, or_3_out, or_5_out, or_7_out;

  Multiplexer #(.width(4)) multiplexer_1 (.in1(in_1), .out(multiplexer_1_out), .sel(PULSANTE));  // open: in0, en
  Multiplexer #(.width(4)) multiplexer_2 (.in1(in_3), .out(multiplexer_2_out), .sel(PULSANTE));  // open: in0, en
  Multiplexer #(.width(4)) multiplexer_3 (.in1(in_6), .out(multiplexer_3_out), .sel(PULSANTE));  // open: in0, en
  Multiplexer #(.width(4)) multiplexer_4 (.in1(in_8), .out(multiplexer_4_out), .sel(PULSANTE));  // open: in0, en
  Comparator #(.width(4)) comparator_1 (.a(C3), .b(D3), .eq(comparator_1_eq));  // open: gt, lt
  Comparator #(.width(4)) comparator_2 (.a(C3), .b(D1), .eq(comparator_2_eq));  // open: gt, lt
  Comparator #(.width(4)) comparator_3 (.a(C3), .b(D2), .eq(comparator_3_eq));  // open: gt, lt
  Comparator #(.width(4)) comparator_4 (.a(C3), .b(D4), .eq(comparator_4_eq));  // open: gt, lt
  Comparator #(.width(4)) comparator_5 (.a(C1), .b(D1), .eq(C1_D1));  // open: gt, lt
  Comparator #(.width(4)) comparator_6 (.a(C1), .b(D2), .eq(comparator_6_eq));  // open: gt, lt
  Comparator #(.width(4)) comparator_7 (.a(C1), .b(D3), .eq(comparator_7_eq));  // open: gt, lt
  Comparator #(.width(4)) comparator_8 (.a(C1), .b(D4), .eq(comparator_8_eq));  // open: gt, lt
  and and_1 (C3_D3, comparator_1_eq, ~C1_D3, ~C2_D3);  // AND_Gate
  and and_2 (and_2_out, comparator_2_eq, ~C1_D1, ~C2_D1);  // AND_Gate
  and and_3 (and_3_out, comparator_3_eq, ~C1_D2, ~C2_D2);  // AND_Gate
  and and_4 (and_4_out, comparator_4_eq, ~C1_D4, ~C2_D4);  // AND_Gate
  D_Flip_Flop d_ff_1 (.Q(C1[3]), .preset(multiplexer_1_out[3]), .reset(RESET));  // open: clk, D, Qn, en
  D_Flip_Flop d_ff_2 (.Q(C2[3]), .preset(multiplexer_2_out[3]), .reset(RESET));  // open: clk, D, Qn, en
  D_Flip_Flop d_ff_3 (.Q(C3[3]), .preset(multiplexer_3_out[3]), .reset(RESET));  // open: clk, D, Qn, en
  D_Flip_Flop d_ff_4 (.Q(C4[3]), .preset(multiplexer_4_out[3]), .reset(RESET));  // open: clk, D, Qn, en
  Multiplexer #(.width(4)) multiplexer_5 (.in0(4'b0000), .in1(D1), .out(multiplexer_5_out), .sel(C1_D1));  // open: en
  Multiplexer #(.width(4)) multiplexer_6 (.in0(4'b0000), .in1(D1), .out(multiplexer_6_out), .sel(C2_D1));  // open: en
  Multiplexer #(.width(4)) multiplexer_7 (.in0(4'b0000), .in1(D1), .out(multiplexer_7_out), .sel(C3_D1));  // open: en
  Multiplexer #(.width(4)) multiplexer_8 (.in0(4'b0000), .in1(D2), .out(multiplexer_8_out), .sel(C1_D2));  // open: en
  Multiplexer #(.width(4)) multiplexer_9 (.in0(4'b0000), .in1(D2), .out(multiplexer_9_out), .sel(C2_D2));  // open: en
  Multiplexer #(.width(4)) multiplexer_10 (.in0(4'b0000), .in1(D2), .out(multiplexer_10_out), .sel(C3_D2));  // open: en
  Multiplexer #(.width(4)) multiplexer_11 (.in0(4'b0000), .in1(D3), .out(multiplexer_11_out), .sel(C1_D3));  // open: en
  Multiplexer #(.width(4)) multiplexer_12 (.in0(4'b0000), .in1(D3), .out(multiplexer_12_out), .sel(C2_D3));  // open: en
  Multiplexer #(.width(4)) multiplexer_13 (.in0(4'b0000), .in1(D3), .out(multiplexer_13_out), .sel(C3_D3));  // open: en
  Multiplexer #(.width(4)) multiplexer_14 (.in0(4'b0000), .in1(D4), .out(multiplexer_14_out), .sel(C1_D4));  // open: en
  Multiplexer #(.width(4)) multiplexer_15 (.in0(4'b0000), .in1(D4), .out(multiplexer_15_out), .sel(C2_D4));  // open: en
  Multiplexer #(.width(4)) multiplexer_16 (.in0(4'b0000), .in1(D4), .out(multiplexer_16_out), .sel(C3_D4));  // open: en
  D_Flip_Flop d_ff_5 (.Q(C1[2]), .preset(multiplexer_1_out[2]), .reset(RESET));  // open: clk, D, Qn, en
  D_Flip_Flop d_ff_6 (.Q(C2[2]), .preset(multiplexer_2_out[2]), .reset(RESET));  // open: clk, D, Qn, en
  D_Flip_Flop d_ff_7 (.Q(C3[2]), .preset(multiplexer_3_out[2]), .reset(RESET));  // open: clk, D, Qn, en
  D_Flip_Flop d_ff_8 (.Q(C4[2]), .preset(multiplexer_4_out[2]), .reset(RESET));  // open: clk, D, Qn, en
  and and_5 (C3_D1, ~C3_D3, and_2_out);  // AND_Gate
  Multiplexer #(.width(4)) multiplexer_17 (.in0(4'b0000), .in1(D1), .out(multiplexer_17_out), .sel(C4_D1));  // open: en
  Multiplexer #(.width(4)) multiplexer_18 (.in0(4'b0000), .in1(D2), .out(multiplexer_18_out), .sel(C4_D2));  // open: en
  Multiplexer #(.width(4)) multiplexer_19 (.in0(4'b0000), .in1(D3), .out(multiplexer_19_out), .sel(C4_D3));  // open: en
  Multiplexer #(.width(4)) multiplexer_20 (.in0(4'b0000), .in1(D4), .out(multiplexer_20_out), .sel(C4_D4));  // open: en
  D_Flip_Flop d_ff_9 (.Q(C1[1]), .preset(multiplexer_1_out[1]), .reset(RESET));  // open: clk, D, Qn, en
  D_Flip_Flop d_ff_10 (.Q(C2[1]), .preset(multiplexer_2_out[1]), .reset(RESET));  // open: clk, D, Qn, en
  D_Flip_Flop d_ff_11 (.Q(C3[1]), .preset(multiplexer_3_out[1]), .reset(RESET));  // open: clk, D, Qn, en
  D_Flip_Flop d_ff_12 (.Q(C4[1]), .preset(multiplexer_4_out[1]), .reset(RESET));  // open: clk, D, Qn, en
  and and_6 (C1_D2, ~C1_D1, comparator_6_eq);  // AND_Gate
  and and_7 (C1_D3, ~C1_D1, ~C1_D2, comparator_7_eq);  // AND_Gate
  and and_8 (C3_D2, ~C3_D3, ~C3_D1, and_3_out);  // AND_Gate
  assign or_1_out = multiplexer_5_out | multiplexer_6_out | multiplexer_7_out | multiplexer_17_out;  // OR_Gate or_1, 4 bits wide
  or or_2 (or_2_out, C1_D1, C2_D1, C3_D1, C4_D1);
  assign or_3_out = multiplexer_8_out | multiplexer_9_out | multiplexer_10_out | multiplexer_18_out;  // OR_Gate or_3, 4 bits wide
  or or_4 (or_4_out, C1_D2, C2_D2, C3_D2, C4_D2);
  assign or_5_out = multiplexer_11_out | multiplexer_12_out | multiplexer_13_out | multiplexer_19_out;  // OR_Gate or_5, 4 bits wide
  or or_6 (or_6_out, C1_D3, C2_D3, C3_D3, C4_D3);
  assign or_7_out = multiplexer_14_out | multiplexer_15_out | multiplexer_16_out | multiplexer_20_out;  // OR_Gate or_7, 4 bits wide
  or or_8 (or_8_out, C1_D4, C2_D4, C3_D4, C4_D4);
  D_Flip_Flop d_ff_13 (.Q(C1[0]), .preset(multiplexer_1_out[0]), .reset(RESET));  // open: clk, D, Qn, en
  D_Flip_Flop d_ff_14 (.Q(C2[0]), .preset(multiplexer_2_out[0]), .reset(RESET));  // open: clk, D, Qn, en
  D_Flip_Flop d_ff_15 (.Q(C3[0]), .preset(multiplexer_3_out[0]), .reset(RESET));  // open: clk, D, Qn, en
  D_Flip_Flop d_ff_16 (.Q(C4[0]), .preset(multiplexer_4_out[0]), .reset(RESET));  // open: clk, D, Qn, en
  and and_9 (C3_D4, ~C3_D3, ~C3_D1, ~C3_D2, and_4_out);  // AND_Gate
  Multiplexer #(.width(4)) multiplexer_21 (.in1(or_1_out), .out(out_11), .sel(or_2_out));  // open: in0, en
  Multiplexer #(.width(4)) multiplexer_22 (.in1(or_3_out), .out(out_12), .sel(or_4_out));  // open: in0, en
  Multiplexer #(.width(4)) multiplexer_23 (.in1(or_5_out), .out(out_13), .sel(or_6_out));  // open: in0, en
  Multiplexer #(.width(4)) multiplexer_24 (.in1(or_7_out), .out(out_14), .sel(or_8_out));  // open: in0, en
  and and_10 (C1_D4, ~C1_D1, ~C1_D2, ~C1_D3, comparator_8_eq);  // AND_Gate
  Multiplexer #(.width(4)) multiplexer_25 (.in1(in_2), .out(multiplexer_25_out), .sel(PULSANTE));  // open: in0, en
  Multiplexer #(.width(4)) multiplexer_26 (.in1(in_4), .out(multiplexer_26_out), .sel(PULSANTE));  // open: in0, en
  Multiplexer #(.width(4)) multiplexer_27 (.in1(in_7), .out(multiplexer_27_out), .sel(PULSANTE));  // open: in0, en
  Multiplexer #(.width(4)) multiplexer_28 (.in1(in_9), .out(multiplexer_28_out), .sel(PULSANTE));  // open: in0, en
  D_Flip_Flop d_ff_17 (.Q(D2[3]), .preset(multiplexer_26_out[3]), .reset(RESET));  // open: clk, D, Qn, en
  D_Flip_Flop d_ff_18 (.Q(D3[3]), .preset(multiplexer_27_out[3]), .reset(RESET));  // open: clk, D, Qn, en
  D_Flip_Flop d_ff_19 (.Q(D4[3]), .preset(multiplexer_28_out[3]), .reset(RESET));  // open: clk, D, Qn, en
  D_Flip_Flop d_ff_20 (.Q(D1[3]), .preset(multiplexer_25_out[3]), .reset(RESET));  // open: clk, D, Qn, en
  D_Flip_Flop d_ff_21 (.Q(D2[2]), .preset(multiplexer_26_out[2]), .reset(RESET));  // open: clk, D, Qn, en
  D_Flip_Flop d_ff_22 (.Q(D3[2]), .preset(multiplexer_27_out[2]), .reset(RESET));  // open: clk, D, Qn, en
  D_Flip_Flop d_ff_23 (.Q(D4[2]), .preset(multiplexer_28_out[2]), .reset(RESET));  // open: clk, D, Qn, en
  Comparator #(.width(4)) comparator_9 (.a(C2), .b(D2), .eq(comparator_9_eq));  // open: gt, lt
  Comparator #(.width(4)) comparator_10 (.a(C2), .b(D1), .eq(comparator_10_eq));  // open: gt, lt
  Comparator #(.width(4)) comparator_11 (.a(C2), .b(D3), .eq(comparator_11_eq));  // open: gt, lt
  Comparator #(.width(4)) comparator_12 (.a(C2), .b(D4), .eq(comparator_12_eq));  // open: gt, lt
  Comparator #(.width(4)) comparator_13 (.a(C4), .b(D4), .eq(comparator_13_eq));  // open: gt, lt
  Comparator #(.width(4)) comparator_14 (.a(C4), .b(D1), .eq(comparator_14_eq));  // open: gt, lt
  Comparator #(.width(4)) comparator_15 (.a(C4), .b(D2), .eq(comparator_15_eq));  // open: gt, lt
  Comparator #(.width(4)) comparator_16 (.a(C4), .b(D3), .eq(comparator_16_eq));  // open: gt, lt
  D_Flip_Flop d_ff_24 (.Q(D1[2]), .preset(multiplexer_25_out[2]), .reset(RESET));  // open: clk, D, Qn, en
  D_Flip_Flop d_ff_25 (.Q(D2[1]), .preset(multiplexer_26_out[1]), .reset(RESET));  // open: clk, D, Qn, en
  D_Flip_Flop d_ff_26 (.Q(D3[1]), .preset(multiplexer_27_out[1]), .reset(RESET));  // open: clk, D, Qn, en
  D_Flip_Flop d_ff_27 (.Q(D4[1]), .preset(multiplexer_28_out[1]), .reset(RESET));  // open: clk, D, Qn, en
  and and_11 (C2_D2, comparator_9_eq, ~C1_D2);  // AND_Gate
  and and_12 (and_12_out, comparator_10_eq, ~C1_D1);  // AND_Gate
  and and_13 (and_13_out, comparator_11_eq, ~C1_D3);  // AND_Gate
  and and_14 (and_14_out, comparator_12_eq, ~C1_D4);  // AND_Gate
  D_Flip_Flop d_ff_28 (.Q(D1[1]), .preset(multiplexer_25_out[1]), .reset(RESET));  // open: clk, D, Qn, en
  D_Flip_Flop d_ff_29 (.Q(D2[0]), .preset(multiplexer_26_out[0]), .reset(RESET));  // open: clk, D, Qn, en
  D_Flip_Flop d_ff_30 (.Q(D3[0]), .preset(multiplexer_27_out[0]), .reset(RESET));  // open: clk, D, Qn, en
  D_Flip_Flop d_ff_31 (.Q(D4[0]), .preset(multiplexer_28_out[0]), .reset(RESET));  // open: clk, D, Qn, en
  and and_15 (C4_D4, comparator_13_eq, ~C1_D4, ~C2_D4, ~C3_D4);  // AND_Gate
  and and_16 (and_16_out, comparator_14_eq, ~C1_D1, ~C2_D1, ~C3_D1);  // AND_Gate
  and and_17 (and_17_out, comparator_15_eq, ~C1_D2, ~C2_D2, ~C3_D2);  // AND_Gate
  and and_18 (and_18_out, comparator_16_eq, ~C1_D3, ~C2_D3, ~C3_D3);  // AND_Gate
  D_Flip_Flop d_ff_32 (.Q(D1[0]), .preset(multiplexer_25_out[0]), .reset(RESET));  // open: clk, D, Qn, en
  and and_19 (C2_D1, ~C2_D2, and_12_out);  // AND_Gate
  and and_20 (C2_D3, ~C2_D2, ~C2_D1, and_13_out);  // AND_Gate
  and and_21 (C4_D1, ~C4_D4, and_16_out);  // AND_Gate
  and and_22 (C2_D4, ~C2_D2, ~C2_D1, ~C2_D3, and_14_out);  // AND_Gate
  and and_23 (C4_D2, ~C4_D4, ~C4_D1, and_17_out);  // AND_Gate
  and and_24 (C4_D3, ~C4_D4, ~C4_D1, ~C4_D2, and_18_out);  // AND_Gate
endmodule
module Luci (
  input  VERDE_1,
  input  VERDE_2,
  input  VERDE_3,
  input  VERDE_4,
  input  RESET,
  input  ROSSO_1,
  input  ROSSO_2,
  input  ROSSO_3,
  input  ROSSO_4,
  output V2,
  output V3,
  output V1,
  output V4,
  output R2,
  output R3,
  output R1,
  output R4
);

  wire _1_2_2_out, _1_2_3_2_out, _1_2_3_out, _1_2_4_2_out, _1_2_4_out, _1_2_out, _1_3_2_out, _1_3_4_2_out,
       _1_3_4_out, _1_3_out, _1_4_2_out, _1_4_out, _2_3_2_out, _2_3_4_2_out, _2_3_4_out, _2_3_out,
       _3_4_2_out, _3_4_out, _24_2_out, _24_out, d_ff_1_q, d_ff_2_q, d_ff_3_q, d_ff_4_q, d_ff_5_q, d_ff_6_q,
       d_ff_7_q, d_ff_8_q;

  or or_1 (V1, d_ff_1_q, d_ff_2_q, d_ff_3_q, d_ff_5_q);
  D_Flip_Flop d_ff_1 (.Q(d_ff_1_q), .preset(VERDE_1), .reset(RESET));  // open: clk, D, Qn, en
  and _1_2 (_1_2_out, d_ff_1_q, d_ff_2_q);
  D_Flip_Flop d_ff_2 (.Q(d_ff_2_q), .preset(VERDE_2), .reset(RESET));  // open: clk, D, Qn, en
  and _1_3 (_1_3_out, d_ff_1_q, d_ff_3_q);
  and _1_4 (_1_4_out, d_ff_1_q, d_ff_5_q);
  D_Flip_Flop d_ff_3 (.Q(d_ff_3_q), .preset(VERDE_3), .reset(RESET));  // open: clk, D, Qn, en
  or or_2 (R1, d_ff_4_q, d_ff_6_q, d_ff_7_q, d_ff_8_q);
  D_Flip_Flop d_ff_4 (.Q(d_ff_4_q), .preset(ROSSO_1), .reset(RESET));  // open: clk, D, Qn, en
  or or_3 (V2, _1_2_out, _1_3_out, _1_4_out, _2_3_out, _24_out, _3_4_out);
  and _2_3 (_2_3_out, d_ff_2_q, d_ff_3_q);
  D_Flip_Flop d_ff_5 (.Q(d_ff_5_q), .preset(VERDE_4), .reset(RESET));  // open: clk, D, Qn, en
  and _1_2_2 (_1_2_2_out, d_ff_4_q, d_ff_6_q);
  D_Flip_Flop d_ff_6 (.Q(d_ff_6_q), .preset(ROSSO_2), .reset(RESET));  // open: clk, D, Qn, en
  and _24 (_24_out, d_ff_2_q, d_ff_5_q);
  and _1_4_2 (_1_4_2_out, d_ff_4_q, d_ff_8_q);
  and _1_3_2 (_1_3_2_out, d_ff_4_q, d_ff_7_q);
  D_Flip_Flop d_ff_7 (.Q(d_ff_7_q), .preset(ROSSO_3), .reset(RESET));  // open: clk, D, Qn, en
  and _3_4 (_3_4_out, d_ff_3_q, d_ff_5_q);
  and _1_2_3 (_1_2_3_out, d_ff_1_q, d_ff_2_q, d_ff_3_q);
  or or_4 (R2, _1_2_2_out, _1_3_2_out, _1_4_2_out, _2_3_2_out, _24_2_out, _3_4_2_out);
  and _2_3_2 (_2_3_2_out, d_ff_6_q, d_ff_7_q);
  D_Flip_Flop d_ff_8 (.Q(d_ff_8_q), .preset(ROSSO_4), .reset(RESET));  // open: clk, D, Qn, en
  or or_5 (V3, _1_2_3_out, _1_2_4_out, _1_3_4_out, _2_3_4_out);
  and _1_2_4 (_1_2_4_out, d_ff_1_q, d_ff_2_q, d_ff_5_q);
  and _24_2 (_24_2_out, d_ff_6_q, d_ff_8_q);
  and _1_3_4 (_1_3_4_out, d_ff_1_q, d_ff_3_q, d_ff_5_q);
  and _3_4_2 (_3_4_2_out, d_ff_7_q, d_ff_8_q);
  and _1_2_3_2 (_1_2_3_2_out, d_ff_4_q, d_ff_6_q, d_ff_7_q);
  and _2_3_4 (_2_3_4_out, d_ff_2_q, d_ff_3_q, d_ff_5_q);
  or or_6 (R3, _1_2_3_2_out, _1_2_4_2_out, _1_3_4_2_out, _2_3_4_2_out);
  and _1_2_4_2 (_1_2_4_2_out, d_ff_4_q, d_ff_6_q, d_ff_8_q);
  and and_1 (V4, d_ff_1_q, d_ff_2_q, d_ff_3_q, d_ff_5_q);
  and _1_3_4_2 (_1_3_4_2_out, d_ff_4_q, d_ff_7_q, d_ff_8_q);
  and _2_3_4_2 (_2_3_4_2_out, d_ff_6_q, d_ff_7_q, d_ff_8_q);
  and and_2 (R4, d_ff_4_q, d_ff_6_q, d_ff_7_q, d_ff_8_q);
endmodule
